// Logisim project RedirectPipeline - v3.0.circ as structural Verilog: 20 circuits, main circuit newmain
module main (
  output out_1,
  output out_2,
  output out_3,
  output [15:0] out_4
);

  wire alu_1_p8, alusrcb_1_alusrcb, and_1_out, and_2_out, and_3_out, and_4_out, and_5_out, clock_1_out,
       comparator_1_eq, comparator_2_eq, comparator_3_eq, comparator_4_eq, comparator_5_eq, comparator_6_eq,
       comparator_7_eq, comparator_8_eq, comparator_9_eq, comparator_10_eq, comparator_11_eq,
       comparator_12_eq, comparator_13_eq, comparator_14_eq, comparator_15_eq, dmload_1_dmload,
       dmsel_1_dmsel, dmstr_1_dmsel, not_1_out, or_1_out, PCen, registerfile_1_p6, rfw_1_alusrcb, RST;
  wire [3:0] aluop_1_out_3, register_2_q;
  wire [4:0] multiplexer_1_out, multiplexer_3_out, registerfile_1_p8, registerfile_1_p9, rs, rt;
  wire [5:0] funct, OP;
  wire [15:6] imm;
  wire [31:0] alu_1_p2, Aluout, dmdout, extcuit_1_out_4, multiplexer_2_out, multiplexer_4_out,
       multiplexer_5_out, pc, pccuit_1_newpc, rfd1, rfd2, rfdin_1_p6;
  wire [31:4] register_2_q_2;

  // Probe on OP
  Clock clock_1 (.out(clock_1_out));
  // Probe on rs
  // Probe on {imm, funct}
  Register #(.width(32)) register_1 (.D(pccuit_1_newpc), .en(PCen), .Q(pc), .clk(clock_1_out), .clr(RST));
  Comparator #(.width(6)) comparator_1 (.a(OP), .b(6'b000011), .eq(comparator_1_eq));  // open: gt, lt
  Button button_1 (.out(RST));
  Counter #(.width(16), .max('hffff)) counter_1 (
    .load(RST), .D({16{1'b0}}), .count(PCen), .Q(out_4), .clk(clock_1_out), .clr(RST));  // open: carry
  // Probe on imm[15:11]
  // Probe on rt
  pccuit pccuit_1 (
    .op(OP), .pc(pc), .Aluout(Aluout), .label({rs, rt, imm, funct}), .rfd1(rfd1), .funct(funct),
    .newpc(pccuit_1_newpc));  // open: out_9, 有条件总数, 无条件总数, 有条件成功总数, clk, pcen
  Multiplexer #(.width(5)) multiplexer_1 (
    .in0(multiplexer_3_out), .in1({5{1'b1}}), .out(multiplexer_1_out), .sel(comparator_1_eq));  // open: en
  // Probe on out_4
  // Probe on imm[10:6]
  // Probe on funct
  ROM #(.addrWidth(24), .dataWidth(32)) rom_1 (.addr({2'b00, pc[23:2]}), .data({OP, rs, rt, imm, funct}));  // open: sel
  Comparator #(.width(6)) comparator_2 (.a(OP), .b(6'b001111), .eq(comparator_2_eq));  // open: gt, lt
  // Probe on {rs, rt, imm, funct}
  Multiplexer #(.width(32)) multiplexer_2 (
    .in0(rfdin_1_p6), .in1({imm, funct, {16{1'b0}}}), .out(multiplexer_2_out), .sel(comparator_2_eq));  // open: en
  Multiplexer #(.width(5)) multiplexer_3 (
    .in0(rt), .in1(imm[15:11]), .out(multiplexer_3_out), .sel(comparator_3_eq));  // open: en
  Extcuit extcuit_1 (.imm({imm, funct}), .op(OP), .funct(funct), .out_4(extcuit_1_out_4));
  Comparator #(.width(6)) comparator_3 (.a({6{1'b0}}), .b(OP), .eq(comparator_3_eq));  // open: gt, lt
  // Rfdin rfdin_1: pin names not known; wires that end beside it: OP, funct, dmdout, Aluout, pc, rfdin_1_p6, rfdin_1_p6
  Rfw rfw_1 (.op(OP), .funct(funct), .AlusrcB(rfw_1_alusrcb));
  Comparator #(.width(1)) comparator_4 (.a(and_3_out), .b(1'b1), .eq(comparator_4_eq));  // open: gt, lt
  not not_1 (not_1_out, comparator_5_eq);
  Comparator #(.width(32)) comparator_5 (.a(rfd1), .b(32'ha), .eq(comparator_5_eq));  // open: gt, lt
  // RegisterFile registerfile_1: pin names not known; wires that end beside it: {rs, rt, imm, funct}, multiplexer_2_out, clock_1_out, rfw_1_alusrcb, multiplexer_1_out, registerfile_1_p6, registerfile_1_p6, registerfile_1_p8, registerfile_1_p9, rfd1, rfd2, rfd1
  and and_1 (and_1_out, comparator_4_eq, not_1_out);
  Comparator #(.width(6)) comparator_6 (.a(funct), .b({6{1'b0}}), .eq(comparator_6_eq));  // open: gt, lt
  Comparator #(.width(6)) comparator_7 (.a(funct), .b(6'b000010), .eq(comparator_7_eq));  // open: gt, lt
  Comparator #(.width(6)) comparator_8 (.a(funct), .b(6'b000011), .eq(comparator_8_eq));  // open: gt, lt
  Comparator #(.width(6)) comparator_9 (.a(funct), .b(6'b000110), .eq(comparator_9_eq));  // open: gt, lt
  Comparator #(.width(6)) comparator_10 (.a(OP), .b({6{1'b0}}), .eq(comparator_10_eq));  // open: gt, lt
  Multiplexer #(.width(32)) multiplexer_4 (
    .in0(rfd1), .in1(rfd2), .out(multiplexer_4_out), .sel(and_4_out));  // open: en
  Aluop aluop_1 (.funct(funct), .op(OP), .out_3(aluop_1_out_3));
  Comparator #(.width(6)) comparator_11 (.a(funct), .b(6'b001100), .eq(comparator_11_eq));  // open: gt, lt
  Comparator #(.width(6)) comparator_12 (.a(OP), .b({6{1'b0}}), .eq(comparator_12_eq));  // open: gt, lt
  Hex_Digit_Display hex_digit_display_1 (.value(register_2_q_2[31:28]));  // open: dp
  Register #(.width(32)) register_2 (
    .D(rfd2), .en(and_1_out), .Q({register_2_q_2, register_2_q}), .clk(clock_1_out), .clr(RST));
  and and_2 (and_2_out, comparator_4_eq, comparator_5_eq);
  not not_2 (PCen, and_2_out);
  or or_1 (or_1_out, comparator_6_eq, comparator_7_eq, comparator_8_eq, comparator_9_eq);
  Multiplexer #(.width(32)) multiplexer_5 (
    .in0(rfd2), .in1(extcuit_1_out_4), .out(multiplexer_5_out), .sel(alusrcb_1_alusrcb));  // open: en
  AlusrcB alusrcb_1 (.op(OP), .funct(funct), .AlusrcB(alusrcb_1_alusrcb));
  and and_3 (and_3_out, comparator_11_eq, comparator_12_eq);
  Hex_Digit_Display hex_digit_display_2 (.value(register_2_q_2[23:20]));  // open: dp
  Hex_Digit_Display hex_digit_display_3 (.value(register_2_q_2[27:24]));  // open: dp
  // ALU alu_1: pin names not known; wires that end beside it: multiplexer_4_out, alu_1_p2, out_1, aluop_1_out_3, out_2, out_3, Aluout, alu_1_p8
  Multiplexer #(.width(5)) multiplexer_6 (
    .in0(rs), .in1(5'b00010), .out(registerfile_1_p8), .sel(and_3_out));  // open: en
  Multiplexer #(.width(5)) multiplexer_7 (
    .in0(rt), .in1(5'b00100), .out(registerfile_1_p9), .sel(and_3_out));  // open: en
  Hex_Digit_Display hex_digit_display_4 (.value(register_2_q_2[19:16]));  // open: dp
  Hex_Digit_Display hex_digit_display_5 (.value(register_2_q_2[15:12]));  // open: dp
  Comparator #(.width(6)) comparator_13 (.a(OP), .b({6{1'b0}}), .eq(comparator_13_eq));  // open: gt, lt
  Comparator #(.width(6)) comparator_14 (.a(funct), .b(6'b000110), .eq(comparator_14_eq));  // open: gt, lt
  and and_4 (and_4_out, or_1_out, comparator_10_eq);
  Dmload dmload_1 (.op(OP), .Dmload(dmload_1_dmload));
  Dmsel dmsel_1 (.op(OP), .Dmsel(dmsel_1_dmsel));
  Dmstr dmstr_1 (.op(OP), .Dmsel(dmstr_1_dmsel));
  Hex_Digit_Display hex_digit_display_6 (.value(register_2_q_2[11:8]));  // open: dp
  Hex_Digit_Display hex_digit_display_7 (.value(register_2_q_2[7:4]));  // open: dp
  // Probe on Aluout
  RAM #(.addrWidth(24), .dataWidth(32), .bus("separate")) ram_1 (
    .addr(Aluout[23:0]), .din(rfd2), .data(dmdout), .str(dmload_1_dmload), .sel(dmsel_1_dmsel),
    .clk(clock_1_out), .ld(dmstr_1_dmsel), .clr(RST));
  Comparator #(.width(6)) comparator_15 (.a(OP), .b(6'b101011), .eq(comparator_15_eq));  // open: gt, lt
  Hex_Digit_Display hex_digit_display_8 (.value(register_2_q));  // open: dp
  and and_5 (and_5_out, comparator_13_eq, comparator_14_eq);
  Multiplexer #(.width(32)) multiplexer_8 (
    .in0(multiplexer_5_out), .in1(rfd1), .out(alu_1_p2), .sel(and_5_out));  // open: en
  not not_3 (alu_1_p8, comparator_15_eq);

  // Other names for the same wires on the sheet: imm[5:0] = funct; shdmt[4:0] = imm[10:6]; rd[4:0] = imm[15:11]

  // Notes on the sheet:
  //         总复位
  //   contents of rom_1 (hex, n*v repeats v):
  //   20110001 8000c05 20110001 20120002 20130003 8000c09 20110001 20120002 20130003 8000c0d 20110001
  //   20120002 20130003 8000c11 20110001 20120002 20130003 c000cb8 20100001 20110001 118fc0 112020
  //   20020022 c 118882 12200001 8000c15 112020 20020022 c 20110001 118880 112020 20020022 c 12200001
  //   8000c1f 20110001 118fc0 112020 20020022 c 1188c3 112020 20020022 c 118903 112020 20020022 c 118903
  //   112020 20020022 c 118903 112020 20020022 c 118903 112020 20020022 c 118903 112020 20020022 c 118903
  //   112020 20020022 c 118903 112020 20020022 c 20100001 109fc0 139fc3 8021 2012000c 24160003 26100001
  //   3210000f 20080008 20090001 139900 2709825 132020 20020022 c 1094022 1500fff9 22100001 2018000f
  //   2188024 108700 20080008 20090001 139902 2709825 132021 20020022 c 1094022 1500fff9 108702 2c9b022
  //   12c00001 8000c50 4020 1084027 84400 3508ffff 82021 20020022 c 2010ffff 20110000 ae300000 22100001
  //   22310004 ae300000 22100001 22310004 ae300000 22100001 22310004 ae300000 22100001 22310004 ae300000
  //   22100001 22310004 ae300000 22100001 22310004 ae300000 22100001 22310004 ae300000 22100001 22310004
  //   ae300000 22100001 22310004 ae300000 22100001 22310004 ae300000 22100001 22310004 ae300000 22100001
  //   22310004 ae300000 22100001 22310004 ae300000 22100001 22310004 ae300000 22100001 22310004 ae300000
  //   22100001 22310004 22100001 8020 2011003c 8e130000 8e340000 274402a 11000002 ae330000 ae140000
  //   2231fffc 1611fff8 102020 20020022 c 22100004 2011003c 1611fff2 2002000a c 20100000 22100001 102020
  //   20020022 c 22100002 102020 20020022 c 22100003 102020 20020022 c 22100004 102020 20020022 c 22100005
  //   102020 20020022 c 22100006 102020 20020022 c 22100007 102020 20020022 c 22100008 102020 20020022
  //   20020022 c 3e00008
endmodule

module Extcuit (
  input  [15:0] imm,
  input  [5:0] op,
  input  [5:0] funct,
  output [31:0] out_4
);

  wire comparator_1_eq, comparator_2_eq, comparator_3_eq, comparator_4_eq, comparator_5_eq, comparator_6_eq,
       comparator_7_eq, comparator_8_eq, comparator_9_eq, comparator_10_eq, comparator_11_eq,
       comparator_12_eq, comparator_13_eq, comparator_14_eq, or_2_out;
  wire [2:0] or_1_out;
  wire [31:0] bit_extender_1_out, bit_extender_2_out, multiplexer_1_out;

  Comparator #(.width(6)) comparator_1 (.a(6'b001000), .b(op), .eq(comparator_1_eq));  // open: gt, lt
  Comparator #(.width(6)) comparator_2 (.a(6'b001001), .b(op), .eq(comparator_2_eq));  // open: gt, lt
  Comparator #(.width(6)) comparator_3 (.a(6'b100011), .b(op), .eq(comparator_3_eq));  // open: gt, lt
  Comparator #(.width(6)) comparator_4 (.a(6'b101011), .b(op), .eq(comparator_4_eq));  // open: gt, lt
  Comparator #(.width(6)) comparator_5 (.a(6'b001010), .b(op), .eq(comparator_5_eq));  // open: gt, lt
  Comparator #(.width(6)) comparator_6 (.a(op), .b(6'b100100), .eq(comparator_6_eq));  // open: gt, lt
  Comparator #(.width(6)) comparator_7 (.a({6{1'b0}}), .b(funct), .eq(comparator_7_eq));  // open: gt, lt
  Comparator #(.width(6)) comparator_8 (.a(6'b000010), .b(funct), .eq(comparator_8_eq));  // open: gt, lt
  Comparator #(.width(6)) comparator_9 (.a(6'b000011), .b(funct), .eq(comparator_9_eq));  // open: gt, lt
  Comparator #(.width(6)) comparator_10 (.a({6{1'b0}}), .b(op), .eq(comparator_10_eq));  // open: gt, lt
  Comparator #(.width(6)) comparator_11 (.a(6'b001100), .b(op), .eq(comparator_11_eq));  // open: gt, lt
  Comparator #(.width(6)) comparator_12 (.a(6'b001101), .b(op), .eq(comparator_12_eq));  // open: gt, lt
  Comparator #(.width(6)) comparator_13 (.a(6'b001110), .b(op), .eq(comparator_13_eq));  // open: gt, lt
  or or_1 (or_1_out[0], comparator_3_eq, comparator_1_eq, comparator_2_eq, comparator_4_eq, comparator_5_eq, comparator_6_eq);
  or or_2 (or_2_out, comparator_7_eq, comparator_8_eq, comparator_9_eq);
  or or_3 (or_1_out[1], comparator_11_eq, comparator_13_eq, comparator_12_eq);
  and and_1 (or_1_out[2], or_2_out, comparator_10_eq);
  assign bit_extender_1_out = {{16{imm[15]}}, imm};  // Bit_Extender bit_extender_1
  assign bit_extender_2_out = {{16{1'b0}}, imm};  // Bit_Extender bit_extender_2
  Multiplexer #(.select(3), .width(32)) multiplexer_1 (
    .in1(bit_extender_1_out), .in2(bit_extender_2_out), .in4({{27{1'b0}}, imm[10:6]}),
    .out(multiplexer_1_out), .sel(or_1_out));  // open: in0, in3, in5, in6, in7, en
  Comparator #(.width(6)) comparator_14 (.a(6'b000001), .b(op), .eq(comparator_14_eq));  // open: gt, lt
  Multiplexer #(.width(32)) multiplexer_2 (
    .in0(multiplexer_1_out), .in1({32{1'b0}}), .out(out_4), .sel(comparator_14_eq));  // open: en

  // Other names for the same wires on the sheet: data[15:0] = imm
endmodule

module AlusrcB (
  input  [5:0] op,
  input  [5:0] funct,
  output AlusrcB
);

  wire and_1_out, comparator_1_eq, comparator_2_eq, comparator_3_eq, comparator_4_eq, comparator_5_eq,
       comparator_6_eq, comparator_7_eq, comparator_8_eq, comparator_9_eq, comparator_10_eq,
       comparator_11_eq, comparator_12_eq, comparator_13_eq, comparator_14_eq, or_1_out, or_2_out;

  Comparator #(.width(6)) comparator_1 (.a(6'b001001), .b(op), .eq(comparator_1_eq));  // open: gt, lt
  Comparator #(.width(6)) comparator_2 (.a(6'b001000), .b(op), .eq(comparator_2_eq));  // open: gt, lt
  Comparator #(.width(6)) comparator_3 (.a(6'b001100), .b(op), .eq(comparator_3_eq));  // open: gt, lt
  Comparator #(.width(6)) comparator_4 (.a(6'b001101), .b(op), .eq(comparator_4_eq));  // open: gt, lt
  Comparator #(.width(6)) comparator_5 (.a(6'b100011), .b(op), .eq(comparator_5_eq));  // open: gt, lt
  Comparator #(.width(6)) comparator_6 (.a(6'b101011), .b(op), .eq(comparator_6_eq));  // open: gt, lt
  Comparator #(.width(6)) comparator_7 (.a(6'b001010), .b(op), .eq(comparator_7_eq));  // open: gt, lt
  Comparator #(.width(6)) comparator_8 (.a(op), .b(6'b001110), .eq(comparator_8_eq));  // open: gt, lt
  Comparator #(.width(6)) comparator_9 (.a(op), .b(6'b100100), .eq(comparator_9_eq));  // open: gt, lt
  or or_1 (or_1_out, comparator_1_eq, comparator_4_eq, comparator_2_eq, comparator_3_eq, comparator_9_eq, comparator_5_eq, comparator_6_eq, comparator_8_eq, comparator_7_eq);
  Comparator #(.width(6)) comparator_10 (.a(op), .b({6{1'b0}}), .eq(comparator_10_eq));  // open: gt, lt
  Comparator #(.width(6)) comparator_11 (.a({6{1'b0}}), .b(funct), .eq(comparator_11_eq));  // open: gt, lt
  Comparator #(.width(6)) comparator_12 (.a(6'b000011), .b(funct), .eq(comparator_12_eq));  // open: gt, lt
  Comparator #(.width(6)) comparator_13 (.a(6'b000010), .b(funct), .eq(comparator_13_eq));  // open: gt, lt
  Comparator #(.width(6)) comparator_14 (.a(funct), .b(6'b000110), .eq(comparator_14_eq));  // open: gt, lt
  Comparator #(.width(6)) comparator_15 ();  // open: a, b, gt, eq, lt
  Comparator #(.width(6)) comparator_16 ();  // open: a, b, gt, eq, lt
  or or_2 (or_2_out, comparator_11_eq, comparator_12_eq, comparator_13_eq);
  and and_1 (and_1_out, comparator_10_eq, or_2_out);
  or or_3 (AlusrcB, and_1_out, or_1_out);
endmodule

// imm
module Rfdin (
  input  [1:0] sel,
  input  [5:0] op,
  input  [5:0] funct,
  input  [31:0] dmout,
  input  [31:0] Aluout,
  input  [31:0] pc,
  input  [15:0] imm,
  output [31:0] out_8
);

  wire comparator_4_eq;
  wire [2:0] comparator_1_eq;
  wire [31:0] adder_1_out, and_2_out, multiplexer_1_out, shifter_1_out;

  Adder #(.width(32)) adder_1 (.a(pc), .b(32'h4), .out(adder_1_out));  // open: cin, cout
  Shifter #(.width(32), .shift("lr")) shifter_1 (.in(dmout), .\dist ({sel, 3'b000}), .out(shifter_1_out));
  Comparator #(.width(6)) comparator_1 (.a(op), .b(6'b100100), .eq(comparator_1_eq[0]));  // open: gt, lt
  Comparator #(.width(6)) comparator_2 (.a(op), .b(6'b100011), .eq(comparator_1_eq[1]));  // open: gt, lt
  Comparator #(.width(6)) comparator_3 (.a(op), .b(6'b000011), .eq(comparator_1_eq[2]));  // open: gt, lt
  // AND_Gate and_1 has open pins: in0=dmout, in1=32'hff, out=open
  assign and_2_out = shifter_1_out & 32'hff;  // AND_Gate and_2, 32 bits wide
  Multiplexer #(.select(3), .width(32)) multiplexer_1 (
    .in0(Aluout), .in1(and_2_out), .in2(dmout), .in3(Aluout), .in4(adder_1_out), .in5(Aluout), .in6(Aluout),
    .in7(Aluout), .out(multiplexer_1_out), .sel(comparator_1_eq));  // open: en
  Comparator #(.width(6)) comparator_4 (.a(op), .b(6'b001111), .eq(comparator_4_eq));  // open: gt, lt
  Multiplexer #(.width(32)) multiplexer_2 (
    .in0(multiplexer_1_out), .in1({imm, {16{1'b0}}}), .out(out_8), .sel(comparator_4_eq));  // open: en
endmodule

module Rfw (
  input  [5:0] op,
  input  [5:0] funct,
  output AlusrcB
);

  wire and_1_out, comparator_1_eq, comparator_2_eq, comparator_4_eq, comparator_5_eq, comparator_6_eq,
       comparator_8_eq, comparator_9_eq, comparator_10_eq, or_1_out, or_2_out, or_3_out;
  wire [5:0] undriven, undriven_2;

  Comparator #(.width(6)) comparator_1 (.a(6'b000001), .b(op), .eq(comparator_1_eq));  // open: gt, lt
  Comparator #(.width(6)) comparator_2 (.a(6'b000010), .b(op), .eq(comparator_2_eq));  // open: gt, lt
  Comparator #(.width(6)) comparator_3 (.b(op));  // open: a, gt, eq, lt
  Comparator #(.width(6)) comparator_4 (.a(6'b000100), .b(op), .eq(comparator_4_eq));  // open: gt, lt
  Comparator #(.width(6)) comparator_5 (.a(6'b000101), .b(op), .eq(comparator_5_eq));  // open: gt, lt
  Comparator #(.width(6)) comparator_6 (.a(6'b101011), .b(op), .eq(comparator_6_eq));  // open: gt, lt
  Comparator #(.width(6)) comparator_7 (.b(undriven));  // open: a, gt, eq, lt
  or or_1 (or_1_out, comparator_2_eq, comparator_1_eq, comparator_4_eq, comparator_5_eq, comparator_6_eq);
  Comparator #(.width(6)) comparator_8 (.a(op), .b({6{1'b0}}), .eq(comparator_8_eq));  // open: gt, lt
  Comparator #(.width(6)) comparator_9 (.a(6'b001000), .b(funct), .eq(comparator_9_eq));  // open: gt, lt
  Comparator #(.width(6)) comparator_10 (.a(6'b001100), .b(funct), .eq(comparator_10_eq));  // open: gt, lt
  Comparator #(.width(6)) comparator_11 (.a(undriven_2), .b(funct));  // open: gt, eq, lt
  Comparator #(.width(6)) comparator_12 ();  // open: a, b, gt, eq, lt
  Comparator #(.width(6)) comparator_13 ();  // open: a, b, gt, eq, lt
  Comparator #(.width(6)) comparator_14 ();  // open: a, b, gt, eq, lt
  or or_2 (or_2_out, comparator_9_eq, comparator_10_eq);
  and and_1 (and_1_out, comparator_8_eq, or_2_out);
  or or_3 (or_3_out, and_1_out, or_1_out);
  not not_1 (AlusrcB, or_3_out);
endmodule

module Dmsel (
  input  [5:0] op,
  output Dmsel
);

  wire comparator_1_eq, comparator_2_eq, comparator_3_eq;

  Comparator #(.width(6)) comparator_1 (.a(op), .b(6'b100011), .eq(comparator_1_eq));  // open: gt, lt
  Comparator #(.width(6)) comparator_2 (.a(op), .b(6'b100100), .eq(comparator_2_eq));  // open: gt, lt
  Comparator #(.width(6)) comparator_3 (.a(op), .b(6'b101011), .eq(comparator_3_eq));  // open: gt, lt
  or or_1 (Dmsel, comparator_1_eq, comparator_2_eq, comparator_3_eq);
endmodule

module pccuit (
  input  [5:0] op,
  input  [31:0] pc,
  input  [31:0] Aluout,
  input  [25:0] label,
  input  [31:0] rfd1,
  input  [5:0] funct,
  input  clk,
  input  pcen,
  output out_9,
  output [31:0] newpc,
  output [15:0] \无条件总数 ,
  output [15:0] \有条件成功总数 ,
  output [15:0] \有条件总数 
);

  wire and_2_out, and_3_out, and_4_out, and_6_out, and_7_out, and_8_out, comparator_1_eq, comparator_2_eq,
       comparator_3_eq, comparator_4_eq, comparator_5_eq, comparator_6_eq, comparator_7_eq, comparator_8_eq,
       comparator_9_eq, comparator_10_eq, comparator_11_eq, cond, not_1_out, or_4_out;
  wire [2:0] and_5_out;
  wire [17:0] and_1_out, shifter_1_out;
  wire [25:0] shifter_2_out;
  wire [31:0] adder_1_out, adder_2_out, bit_extender_1_out, bit_extender_2_out, subtractor_1_out;

  assign and_1_out = label[17:0] & 18'hffff;  // AND_Gate and_1, 18 bits wide
  Adder #(.width(32)) adder_1 (.a(pc), .b(32'h4), .out(adder_1_out));  // open: cin, cout
  Comparator #(.width(6)) comparator_1 (.a(op), .b(6'b000010), .eq(comparator_1_eq));  // open: gt, lt
  Comparator #(.width(6)) comparator_2 (.a(op), .b(6'b000011), .eq(comparator_2_eq));  // open: gt, lt
  Shifter #(.width(18)) shifter_1 (.in(and_1_out), .\dist (5'b00010), .out(shifter_1_out));
  Shifter #(.width(26)) shifter_2 (.in(label), .\dist (5'b00010), .out(shifter_2_out));
  assign bit_extender_1_out = {{14{shifter_1_out[17]}}, shifter_1_out};  // Bit_Extender bit_extender_1
  or or_1 (and_5_out[1], comparator_1_eq, comparator_2_eq);
  assign bit_extender_2_out = {{6{shifter_2_out[25]}}, shifter_2_out};  // Bit_Extender bit_extender_2
  Comparator #(.width(32)) comparator_3 (.a(Aluout), .b({32{1'b0}}), .eq(comparator_3_eq));  // open: gt, lt
  Comparator #(.width(6)) comparator_4 (.a(op), .b(6'b000100), .eq(comparator_4_eq));  // open: gt, lt
  Comparator #(.width(6)) comparator_5 (.a(op), .b(6'b000101), .eq(comparator_5_eq));  // open: gt, lt
  Comparator #(.width(32)) comparator_6 (.a(Aluout), .b({32{1'b0}}), .eq(comparator_6_eq));  // open: gt, lt
  not not_1 (not_1_out, comparator_6_eq);
  Adder #(.width(32)) adder_2 (.a(bit_extender_1_out), .b(adder_1_out), .out(adder_2_out));  // open: cin, cout
  and and_2 (and_2_out, comparator_3_eq, comparator_4_eq);
  or or_2 (cond, comparator_4_eq, comparator_5_eq);
  and and_3 (and_3_out, comparator_5_eq, not_1_out);
  Comparator #(.width(32)) comparator_7 (.a(Aluout), .b(32'h1), .eq(comparator_7_eq));  // open: gt, lt
  Comparator #(.width(6)) comparator_8 (.a(op), .b(6'b000001), .eq(comparator_8_eq));  // open: gt, lt
  Subtractor #(.width(32)) subtractor_1 (
    .a({pc[31:28], label, 2'b00}), .b(32'h3000), .out(subtractor_1_out));  // open: bin, bout
  Comparator #(.width(6)) comparator_9 (.a(op), .b({6{1'b0}}), .eq(comparator_9_eq));  // open: gt, lt
  Comparator #(.width(6)) comparator_10 (.a(funct), .b(6'b001000), .eq(comparator_10_eq));  // open: gt, lt
  and and_4 (and_4_out, comparator_7_eq, comparator_8_eq);
  or or_3 (and_5_out[2], and_2_out, and_4_out, and_3_out);
  and and_5 (and_5_out[0], comparator_9_eq, comparator_10_eq);
  Multiplexer #(.select(3), .width(32)) multiplexer_1 (
    .in0(adder_1_out), .in1(rfd1), .in2(subtractor_1_out), .in3(adder_1_out), .in4(adder_2_out),
    .in5(adder_1_out), .in6(adder_1_out), .in7(adder_1_out), .out(newpc), .sel(and_5_out));  // open: en
  and and_6 (and_6_out, pcen, cond);
  Counter #(.width(16), .max('hffff)) counter_1 (
    .count(and_6_out), .Q(\有条件总数 ), .clk(clk));  // open: load, D, carry, clr
  Comparator #(.width(32)) comparator_11 (.a(adder_1_out), .b(newpc), .eq(comparator_11_eq));  // open: gt, lt
  not not_2 (out_9, comparator_11_eq);
  Counter #(.width(16), .max('hffff)) counter_2 (
    .count(and_7_out), .Q(\无条件总数 ), .clk(clk));  // open: load, D, carry, clr
  and and_7 (and_7_out, pcen, or_4_out);
  or or_4 (or_4_out, and_5_out[1], and_5_out[0]);
  and and_8 (and_8_out, pcen, and_5_out[2]);
  Counter #(.width(16), .max('hffff)) counter_3 (
    .count(and_8_out), .Q(\有条件成功总数 ), .clk(clk));  // open: load, D, carry, clr
endmodule

module test (
);

  wire [23:0] undriven;
  wire [31:0] rom_1_data;

  ROM #(.addrWidth(24), .dataWidth(32)) rom_1 (.addr(undriven), .data(rom_1_data));  // open: sel
endmodule

module Dmload (
  input  [5:0] op,
  output Dmload
);

  Comparator #(.width(6)) comparator_1 (.a(op), .b(6'b101011), .eq(Dmload));  // open: gt, lt
endmodule

module Dmstr (
  input  [5:0] op,
  output Dmsel
);

  wire comparator_1_eq, comparator_2_eq;

  Comparator #(.width(6)) comparator_1 (.a(op), .b(6'b100011), .eq(comparator_1_eq));  // open: gt, lt
  Comparator #(.width(6)) comparator_2 (.a(op), .b(6'b100100), .eq(comparator_2_eq));  // open: gt, lt
  or or_1 (Dmsel, comparator_1_eq, comparator_2_eq);
endmodule

module Aluop (
  input  [5:0] funct,
  input  [5:0] op,
  output [3:0] out_3
);

  wire comparator_1_eq;
  wire [3:0] rom_1_data, rom_2_data;

  Comparator #(.width(6)) comparator_1 (.a({6{1'b0}}), .b(op), .eq(comparator_1_eq));  // open: gt, lt
  ROM #(.addrWidth(6), .dataWidth(4)) rom_1 (.addr(funct), .data(rom_1_data));  // open: sel
  ROM #(.addrWidth(6), .dataWidth(4)) rom_2 (.addr(op), .data(rom_2_data));  // open: sel
  Multiplexer #(.width(4)) multiplexer_1 (
    .in0(rom_2_data), .in1(rom_1_data), .out(out_3), .sel(comparator_1_eq));  // open: en

  // Notes on the sheet:
  //   contents of rom_1 (hex, n*v repeats v):
  //   0 0 2 1 0 0 2 25*0 5 5 6 0 7 8 9 a 0 0 b c
  //   contents of rom_2 (hex, n*v repeats v):
  //   0 b 0 0 9 9 0 0 5 5 b 0 7 8 9 28*0 5
endmodule

module Controller (
  input  [31:0] IR,
  output [5:0] OP,
  output [4:0] rs,
  output [3:0] ALUop,
  output [4:0] rt,
  output [4:0] rd,
  output dmload,
  output [4:0] shdmt,
  output dmstr,
  output [5:0] funct,
  output dmsel,
  output W_num,
  output [4:0] rw,
  output [4:0] rA,
  output [4:0] rB,
  output [15:0] imm
);

  wire and_1_out, comparator_1_eq, comparator_2_eq, comparator_3_eq, comparator_4_eq;
  wire [4:0] multiplexer_1_out;

  // Probe on IR[31:26]
  // Probe on IR[20:16]
  // Probe on IR[25:21]
  Dmstr dmstr_1 (.op(IR[31:26]), .Dmsel(dmload));
  Dmload dmload_1 (.op(IR[31:26]), .Dmload(dmstr));
  Dmsel dmsel_1 (.op(IR[31:26]), .Dmsel(dmsel));
  // Probe on IR[15:11]
  // Probe on IR[10:6]
  // Probe on IR[5:0]
  Aluop aluop_1 (.funct(IR[5:0]), .op(IR[31:26]), .out_3(ALUop));
  Comparator #(.width(6)) comparator_1 (.a(IR[31:26]), .b(6'b000011), .eq(comparator_1_eq));  // open: gt, lt
  Multiplexer #(.width(5)) multiplexer_1 (
    .in0(IR[20:16]), .in1(IR[15:11]), .out(multiplexer_1_out), .sel(comparator_4_eq));  // open: en
  Multiplexer #(.width(5)) multiplexer_2 (
    .in0(multiplexer_1_out), .in1({5{1'b1}}), .out(rw), .sel(comparator_1_eq));  // open: en
  Comparator #(.width(6)) comparator_2 (.a(IR[5:0]), .b(6'b001100), .eq(comparator_2_eq));  // open: gt, lt
  Comparator #(.width(6)) comparator_3 (.a(IR[31:26]), .b({6{1'b0}}), .eq(comparator_3_eq));  // open: gt, lt
  Rfw rfw_1 (.op(IR[31:26]), .funct(IR[5:0]), .AlusrcB(W_num));
  Comparator #(.width(6)) comparator_4 (.a({6{1'b0}}), .b(IR[31:26]), .eq(comparator_4_eq));  // open: gt, lt
  and and_1 (and_1_out, comparator_2_eq, comparator_3_eq);
  Multiplexer #(.width(5)) multiplexer_3 (.in0(IR[25:21]), .in1(5'b00010), .out(rA), .sel(and_1_out));  // open: en
  Multiplexer #(.width(5)) multiplexer_4 (.in0(IR[20:16]), .in1(5'b00100), .out(rB), .sel(and_1_out));  // open: en

  assign funct = IR[5:0];
  assign imm = IR[15:0];
  assign OP = IR[31:26];
  assign rd = IR[15:11];
  assign rs = IR[25:21];
  assign rt = IR[20:16];
  assign shdmt = IR[10:6];
endmodule

module newmain (
  output [15:0] out_1
);

  wire alu_1_p4, alu_1_p9, alusrcb_1_alusrcb, and_1_out, and_2_out, and_3_out, and_4_out, and_5_out,
       and_6_out, and_7_out, and_8_out, and_9_out, clk, clken, comparator_1_eq, comparator_2_eq,
       comparator_3_eq, comparator_4_eq, comparator_5_eq, comparator_6_eq, comparator_7_eq, comparator_8_eq,
       comparator_9_eq, comparator_10_eq, comparator_11_eq, comparator_12_eq, comparator_13_eq,
       comparator_14_eq, comparator_15_eq, comparator_16_eq, comparator_17_eq, comparator_18_eq,
       comparator_19_eq, comparator_20_eq, comparator_21_eq, conflijudge_1_aluaeq, conflijudge_1_alubeq,
       conflijudge_1_memaeq, conflijudge_1_membeq, conflijudge_1_rfd2alueq, conflijudge_1_rfd2dmeq,
       conflijudge_1_src1ex, conflijudge_1_src1mem, controller_1_dmload, controller_1_dmsel,
       controller_1_dmstr, ex_mem_1_dmld_2, ex_mem_1_dmsel_2, ex_mem_1_dmstr_2, id_ex_1_dmld_2,
       id_ex_1_dmsel_2, id_ex_1_dmstr_2, not_1_out, not_2_out, not_3_out, not_4_out, not_5_out, or_1_out,
       or_2_out, or_3_out, PCclear, PCen, registerfile_1_p4, RST, stall;
  wire [1:0] aluselb, id_ex_1_alusela_2, id_ex_1_rfd2sel_2, mem_wb_1_sel_2, register_1_q, rfd1sel, rfd2sel,
       rxxx, sela, selb;
  wire [3:0] controller_1_aluop, id_ex_1_aluop_2, register_2_q;
  wire [4:0] controller_1_ra, controller_1_rb, controller_1_rs, controller_1_rt, controller_1_rw, Memrd,
       Memrt, multiplexer_10_out, parser_3_rt, registerfile_1_p5;
  wire [5:0] Exfunct, ExOP, IDfunct, IDOP, Memfunct, MemOP, parser_3_op;
  wire [7:0] register_1_q_3;
  wire [15:0] condsum, condsusssum, controller_1_imm, parser_3_funct, uncondsum;
  wire [21:0] register_1_q_2;
  wire [23:0] multiplexer_9_out, shifter_1_out;
  wire [25:6] label;
  wire [31:0] adder_1_out, alu_1_p8, alu_1_p11, ex_mem_1_pc_2, ex_mem_1_rfd1_2, ex_mem_1_rfd2_2, EXIR,
       EXRFD1, extcuit_1_out_4, id_ex_1_immext_2, id_ex_1_pc_2, id_ex_1_rfd2_2, if_id_1_ir_2, if_id_1_pc_2,
       mem_wb_1_aluout_2, mem_wb_1_dmdout_2, mem_wb_1_pc_2, MEMAluout, MEMIR, multiplexer_1_out,
       multiplexer_2_out, multiplexer_3_out, multiplexer_4_out, multiplexer_5_out, multiplexer_6_out,
       multiplexer_7_out, multiplexer_8_out, npc, R, ram_1_data, registerfile_1_p9, registerfile_1_p10, RFD1,
       rom_1_data, WBIR, wbout, X, Y;
  wire [31:4] register_2_q_2;

  or or_1 (or_1_out, stall, PCen);
  Clock clock_1 (.out(clk));
  not not_1 (not_1_out, PCen);
  not not_2 (not_2_out, or_1_out);
  Register #(.width(32)) register_1 (
    .D(multiplexer_1_out), .en(not_2_out), .Q({register_1_q_3, register_1_q_2, register_1_q}), .clk(clk),
    .clr(RST));
  Button button_1 (.out(RST));
  Counter #(.width(16), .max('hffff)) counter_1 (
    .load(RST), .D({16{1'b0}}), .count(not_1_out), .Q(out_1), .clk(clk), .clr(RST));  // open: carry
  // Probe on rom_1_data
  // Probe on if_id_1_ir_2
  // Probe on EXIR
  // Probe on MEMIR
  // Probe on WBIR
  Multiplexer #(.width(32)) multiplexer_1 (
    .in0(adder_1_out), .in1(npc), .out(multiplexer_1_out), .sel(PCclear));  // open: en
  Adder #(.width(32)) adder_1 (
    .a({register_1_q_3, register_1_q_2, register_1_q}), .b(32'h4), .out(adder_1_out));  // open: cin, cout
  ROM #(.addrWidth(24), .dataWidth(32)) rom_1 (.addr({2'b00, register_1_q_2}), .data(rom_1_data));  // open: sel
  // Probe on out_1
  // Probe on condsum
  // Probe on uncondsum
  // Probe on condsusssum
  IF_ID if_id_1 (
    .IR(rom_1_data), .IR_2(if_id_1_ir_2), .pc({register_1_q_3, register_1_q_2, register_1_q}),
    .pc_2(if_id_1_pc_2), .stall(not_2_out), .clk(clk), .PCclear(PCclear));  // open: NPC, NPC_2
  // Probe on if_id_1_ir_2
  Comparator #(.width(6)) comparator_1 (.a(Exfunct), .b(6'b001100), .eq(comparator_1_eq));  // open: gt, lt
  Comparator #(.width(6)) comparator_2 (.a(ExOP), .b({6{1'b0}}), .eq(comparator_2_eq));  // open: gt, lt
  Controller controller_1 (
    .IR(if_id_1_ir_2), .ALUop(controller_1_aluop), .dmload(controller_1_dmload), .dmstr(controller_1_dmstr),
    .dmsel(controller_1_dmsel), .rw(controller_1_rw), .rA(controller_1_ra), .rB(controller_1_rb),
    .funct(IDfunct), .OP(IDOP), .rs(controller_1_rs), .rt(controller_1_rt), .imm(controller_1_imm));  // open: W_num, shdmt, rd
  // Probe on wbout
  Comparator #(.width(6)) comparator_3 (.a(IDfunct), .b(6'b001100), .eq(comparator_3_eq));  // open: gt, lt
  Comparator #(.width(6)) comparator_4 (.a(IDOP), .b({6{1'b0}}), .eq(comparator_4_eq));  // open: gt, lt
  Extcuit extcuit_1 (.imm(controller_1_imm), .op(IDOP), .funct(IDfunct), .out_4(extcuit_1_out_4));
  // Probe on controller_1_ra
  // Probe on registerfile_1_p5
  and and_1 (and_1_out, comparator_3_eq, comparator_4_eq);
  and and_2 (and_2_out, comparator_1_eq, comparator_2_eq);
  // Probe on ExOP
  // Probe on controller_1_rb
  Comparator #(.width(1)) comparator_5 (.a(and_1_out), .b(1'b1), .eq(comparator_5_eq));  // open: gt, lt
  Comparator #(.width(32)) comparator_6 (.a(multiplexer_2_out), .b(32'ha), .eq(comparator_6_eq));  // open: gt, lt
  not not_3 (not_3_out, comparator_6_eq);
  Comparator #(.width(1)) comparator_7 (.a(and_2_out), .b(1'b1), .eq(comparator_7_eq));  // open: gt, lt
  ID_EX id_ex_1 (
    .pc(if_id_1_pc_2), .rfd1(registerfile_1_p9), .rfd2(registerfile_1_p10), .pc_2(id_ex_1_pc_2),
    .rfd1_2(EXRFD1), .rfd2_2(id_ex_1_rfd2_2), .immext(extcuit_1_out_4), .immext_2(id_ex_1_immext_2),
    .clk(clk), .dmstr(controller_1_dmstr), .dmstr_2(id_ex_1_dmstr_2), .aluop(controller_1_aluop),
    .aluop_2(id_ex_1_aluop_2), .dmsel(controller_1_dmsel), .dmsel_2(id_ex_1_dmsel_2),
    .dmld(controller_1_dmload), .dmld_2(id_ex_1_dmld_2), .stall(or_2_out), .IR(if_id_1_ir_2), .IR_2(EXIR),
    .alusela(sela), .aluselb(selb), .alusela_2(id_ex_1_alusela_2), .aluselb_2(aluselb), .rfd2sel(rfd2sel),
    .rfd2sel_2(id_ex_1_rfd2sel_2), .rfd1sel(rxxx), .rfd1sel_2(rfd1sel), .in_16(PCen));
  // RegisterFile registerfile_1: pin names not known; wires that end beside it: controller_1_rw, wbout, clk, registerfile_1_p4, registerfile_1_p5, IDOP, controller_1_ra, controller_1_rb, registerfile_1_p9, registerfile_1_p10
  or or_2 (or_2_out, PCclear, stall);
  Multiplexer #(.select(2), .width(32)) multiplexer_2 (
    .in0(EXRFD1), .in1(MEMAluout), .in2(wbout), .out(multiplexer_2_out), .sel(rfd1sel));  // open: in3, en
  and and_3 (and_3_out, comparator_5_eq, not_3_out);
  ConfliJudge conflijudge_1 (
    .IDrt(controller_1_rt), .IDop(IDOP), .IDfunct(IDfunct), .IDrs(controller_1_rs), .EXop(ExOP),
    .EXfunct(Exfunct), .Memop(MemOP), .Memfunct(Memfunct), .EXrd(label[15:11]), .EXrt(label[20:16]),
    .Memrd(Memrd), .Memrt(Memrt), .memaeq(conflijudge_1_memaeq), .membeq(conflijudge_1_membeq),
    .stall(stall), .aluaeq(conflijudge_1_aluaeq), .alubeq(conflijudge_1_alubeq),
    .rfd2alueq(conflijudge_1_rfd2alueq), .rfd2dmeq(conflijudge_1_rfd2dmeq), .src1ex(conflijudge_1_src1ex),
    .src1mem(conflijudge_1_src1mem));
  Comparator #(.width(6)) comparator_8 (.a(Exfunct), .b({6{1'b0}}), .eq(comparator_8_eq));  // open: gt, lt
  Comparator #(.width(6)) comparator_9 (.a(Exfunct), .b(6'b000010), .eq(comparator_9_eq));  // open: gt, lt
  Comparator #(.width(6)) comparator_10 (.a(Exfunct), .b(6'b000011), .eq(comparator_10_eq));  // open: gt, lt
  Comparator #(.width(6)) comparator_11 (.a(Exfunct), .b(6'b000110), .eq(comparator_11_eq));  // open: gt, lt
  Comparator #(.width(6)) comparator_12 (.a(ExOP), .b({6{1'b0}}), .eq(comparator_12_eq));  // open: gt, lt
  // Probe on EXIR
  Register #(.width(32)) register_2 (
    .D(registerfile_1_p10), .en(and_3_out), .Q({register_2_q_2, register_2_q}), .clk(clk), .clr(RST));
  and and_4 (and_4_out, comparator_7_eq, comparator_6_eq);
  or or_3 (or_3_out, comparator_8_eq, comparator_9_eq, comparator_10_eq, comparator_11_eq);
  parser parser_1 (
    .IR(EXIR), .funct(Exfunct), .shamt(label[10:6]), .rd(label[15:11]), .rt(label[20:16]), .rs(label[25:21]),
    .OP(ExOP));
  Multiplexer #(.width(32)) multiplexer_3 (
    .in0(EXRFD1), .in1(id_ex_1_rfd2_2), .out(multiplexer_3_out), .sel(and_5_out));  // open: en
  Multiplexer #(.width(32)) multiplexer_4 (
    .in0(id_ex_1_rfd2_2), .in1(id_ex_1_immext_2), .out(multiplexer_4_out), .sel(alusrcb_1_alusrcb));  // open: en
  AlusrcB alusrcb_1 (.op(ExOP), .funct(Exfunct), .AlusrcB(alusrcb_1_alusrcb));
  Comparator #(.width(6)) comparator_13 (.a(ExOP), .b({6{1'b0}}), .eq(comparator_13_eq));  // open: gt, lt
  Comparator #(.width(6)) comparator_14 (.a(Exfunct), .b(6'b000110), .eq(comparator_14_eq));  // open: gt, lt
  Hex_Digit_Display hex_digit_display_1 (.value(register_2_q_2[31:28]));  // open: dp
  Hex_Digit_Display hex_digit_display_2 (.value(register_2_q_2[27:24]));  // open: dp
  and and_5 (and_5_out, or_3_out, comparator_12_eq);
  not not_4 (not_4_out, PCen);
  pccuit pccuit_1 (
    .op(ExOP), .pc(id_ex_1_pc_2), .Aluout(alu_1_p8), .label({label, Exfunct}), .rfd1(EXRFD1),
    .funct(Exfunct), .newpc(npc), .out_9(PCclear), .\有条件总数 (condsum), .\无条件总数 (uncondsum),
    .\有条件成功总数 (condsusssum), .clk(clk), .pcen(not_4_out));
  Multiplexer #(.select(2), .width(32)) multiplexer_5 (
    .in0(multiplexer_3_out), .in1(MEMAluout), .in2(wbout), .out(multiplexer_5_out), .sel(id_ex_1_alusela_2));  // open: in3, en
  Multiplexer #(.select(2), .width(32)) multiplexer_6 (
    .in0(multiplexer_7_out), .in1(MEMAluout), .in2(wbout), .out(multiplexer_6_out), .sel(aluselb));  // open: in3, en
  Multiplexer #(.width(32)) multiplexer_7 (
    .in0(multiplexer_4_out), .in1(EXRFD1), .out(multiplexer_7_out), .sel(and_6_out));  // open: en
  Hex_Digit_Display hex_digit_display_3 (.value(register_2_q_2[19:16]));  // open: dp
  Hex_Digit_Display hex_digit_display_4 (.value(register_2_q_2[23:20]));  // open: dp
  ALUSrcsel alusrcsel_1 (
    .idsrc1mem(conflijudge_1_src1mem), .idsrc1ex(conflijudge_1_src1ex), .memaeq(conflijudge_1_memaeq),
    .aluaeq(conflijudge_1_aluaeq), .memebeq(conflijudge_1_membeq), .alubeq(conflijudge_1_alubeq),
    .rfd2dmbeq(conflijudge_1_rfd2dmeq), .rfd2alueq(conflijudge_1_rfd2alueq), .rfd1sel(rxxx), .sela(sela),
    .selb(selb), .rfd2sel(rfd2sel));
  // Probe on rxxx
  // ALU alu_1: pin names not known; wires that end beside it: wbout, multiplexer_5_out, multiplexer_6_out, alu_1_p4, alu_1_p4, condsusssum, id_ex_1_aluop_2, alu_1_p8, alu_1_p9, alu_1_p9, alu_1_p11
  // Probe on alu_1_p8
  Multiplexer #(.select(2), .width(32)) multiplexer_8 (
    .in0(id_ex_1_rfd2_2), .in1(MEMAluout), .in2(wbout), .out(multiplexer_8_out), .sel(id_ex_1_rfd2sel_2));  // open: in3, en
  and and_6 (and_6_out, comparator_13_eq, comparator_14_eq);
  Hex_Digit_Display hex_digit_display_5 (.value(register_2_q_2[15:12]));  // open: dp
  Hex_Digit_Display hex_digit_display_6 (.value(register_2_q_2[11:8]));  // open: dp
  Counter #(.width(1), .max('h1)) counter_2 (.Q(PCen), .clk(and_4_out));  // open: load, D, count, carry, clr
  // Probe on MEMAluout
  // Probe on MEMIR
  EX_MEM ex_mem_1 (
    .dmld(id_ex_1_dmld_2), .dmsel(id_ex_1_dmsel_2), .dmstr(id_ex_1_dmstr_2), .aluout(alu_1_p8),
    .rfd1(EXRFD1), .rfd2(multiplexer_8_out), .clk(clk), .rst(RST), .npc_2(alu_1_p11),
    .dmld_2(ex_mem_1_dmld_2), .dmsel_2(ex_mem_1_dmsel_2), .dmstr_2(ex_mem_1_dmstr_2), .aluout_2(MEMAluout),
    .rfd1_2(ex_mem_1_rfd1_2), .rfd2_2(ex_mem_1_rfd2_2), .pc(id_ex_1_pc_2), .pc_2(ex_mem_1_pc_2), .IR(EXIR),
    .IR_2(MEMIR));  // open: npc
  // Probe on ex_mem_1_rfd2_2
  // Probe on X
  Hex_Digit_Display hex_digit_display_7 (.value(register_2_q_2[7:4]));  // open: dp
  Hex_Digit_Display hex_digit_display_8 (.value(register_2_q));  // open: dp
  Shifter #(.width(24), .shift("lr")) shifter_1 (.in(MEMAluout[23:0]), .\dist (5'b00010), .out(shifter_1_out));
  parser parser_2 (.IR(MEMIR), .funct(Memfunct), .rd(Memrd), .rt(Memrt), .OP(MemOP));  // open: shamt, rs
  // Probe on ex_mem_1_dmstr_2
  // Probe on ex_mem_1_dmsel_2
  // Probe on Y
  // Probe on npc
  Multiplexer #(.width(24)) multiplexer_9 (
    .in0(MEMAluout[23:0]), .in1(shifter_1_out), .out(multiplexer_9_out), .sel(comparator_15_eq));  // open: en
  // Probe on ex_mem_1_dmld_2
  // Probe on multiplexer_9_out
  // Probe on R
  Comparator #(.width(6)) comparator_15 (.a(MemOP), .b(6'b100100), .eq(comparator_15_eq));  // open: gt, lt
  // Probe on ram_1_data
  MEM_WB mem_wb_1 (
    .dmdout(ram_1_data), .aluout(MEMAluout), .clk(clk), .dmdout_2(mem_wb_1_dmdout_2),
    .aluout_2(mem_wb_1_aluout_2), .rst(RST), .pc(ex_mem_1_pc_2), .pc_2(mem_wb_1_pc_2),
    .rfd1(ex_mem_1_rfd1_2), .rfd1_2(RFD1), .rfd2(ex_mem_1_rfd2_2), .IR(MEMIR), .IR_2(WBIR),
    .SEL(MEMAluout[1:0]), .SEL_2(mem_wb_1_sel_2));  // open: rfd2_2
  RAM #(.addrWidth(24), .dataWidth(32), .bus("separate")) ram_1 (
    .addr(multiplexer_9_out), .din(ex_mem_1_rfd2_2), .data(ram_1_data), .str(ex_mem_1_dmstr_2),
    .sel(ex_mem_1_dmsel_2), .clk(clk), .ld(ex_mem_1_dmld_2), .clr(RST));
  // Probe on WBIR
  // Probe on mem_wb_1_dmdout_2
  Rfdin rfdin_1 (
    .op(parser_3_op), .funct(parser_3_funct[5:0]), .dmout(mem_wb_1_dmdout_2), .Aluout(mem_wb_1_aluout_2),
    .pc(mem_wb_1_pc_2), .out_8(wbout), .imm(parser_3_funct), .sel(mem_wb_1_sel_2));
  Comparator #(.width(6)) comparator_16 (
    .a(parser_3_funct[5:0]), .b(6'b001100), .eq(comparator_16_eq));  // open: gt, lt
  Comparator #(.width(6)) comparator_17 (.a(parser_3_op), .b({6{1'b0}}), .eq(comparator_17_eq));  // open: gt, lt
  // Probe on mem_wb_1_pc_2
  // Probe on mem_wb_1_aluout_2
  // Probe on parser_3_op
  Rfw rfw_1 (.op(parser_3_op), .funct(parser_3_funct[5:0]), .AlusrcB(registerfile_1_p4));
  // Probe on parser_3_funct
  // Probe on parser_3_funct[15:11]
  // Probe on parser_3_funct[5:0]
  and and_7 (and_7_out, comparator_16_eq, comparator_17_eq);
  // Probe on parser_3_funct[10:6]
  Comparator #(.width(1)) comparator_18 (.a(and_7_out), .b(1'b1), .eq(comparator_18_eq));  // open: gt, lt
  Comparator #(.width(32)) comparator_19 (.a(RFD1), .b(32'ha), .eq(comparator_19_eq));  // open: gt, lt
  parser parser_3 (
    .IR(WBIR), .funct(parser_3_funct[5:0]), .shamt(parser_3_funct[10:6]), .rd(parser_3_funct[15:11]),
    .rt(parser_3_rt), .OP(parser_3_op));  // open: rs
  Multiplexer #(.width(5)) multiplexer_10 (
    .in0(parser_3_rt), .in1(parser_3_funct[15:11]), .out(multiplexer_10_out), .sel(comparator_21_eq));  // open: en
  Comparator #(.width(6)) comparator_20 (.a(parser_3_op), .b(6'b000011), .eq(comparator_20_eq));  // open: gt, lt
  not not_5 (not_5_out, comparator_19_eq);
  Multiplexer #(.width(5)) multiplexer_11 (
    .in0(multiplexer_10_out), .in1({5{1'b1}}), .out(registerfile_1_p5), .sel(comparator_20_eq));  // open: en
  D_Flip_Flop d_ff_1 ();  // open: clk, D, Q, Qn, preset, en, reset
  and and_8 (and_8_out, comparator_18_eq, not_5_out);
  and and_9 (and_9_out, comparator_18_eq, comparator_19_eq);
  Comparator #(.width(6)) comparator_21 (.a({6{1'b0}}), .b(parser_3_op), .eq(comparator_21_eq));  // open: gt, lt
  Register #(.width(1)) register_3 (.D(1'b0));  // open: en, Q, clk, clr
  not not_6 (clken, and_9_out);

  // Other names for the same wires on the sheet: label[5:0] = Exfunct; SEL[1:0] = MEMAluout[1:0]

  // Notes on the sheet:
  //         总复位
  //   contents of rom_1 (hex, n*v repeats v):
  //   20110004 ae310000 8e320000 2252fffc 20100000 22110001 2118020 22520004 ae500000 22310001 2118020
  //   22520004 ae500000 22310001 2118020 22520004 ae500000 22310001 2118020 22520004 ae500000 22310001
  //   2118020 22520004 ae500000 22310001 2118020 22520004 ae500000 22310001 2118020 22520004 ae500000
  //   2002000a 20100000 20100000 20100000 c
endmodule

module IF_ID (
  input  [31:0] pc,
  input  stall,
  input  [31:0] NPC,
  input  [31:0] IR,
  input  clk,
  input  PCclear,
  output [31:0] pc_2,
  output [31:0] NPC_2,
  output [31:0] IR_2
);

  wire and_1_out, register_1_q;

  Register #(.width(1)) register_1 (.D(PCclear), .Q(register_1_q), .clk(clk));  // open: en, clr
  Register #(.width(32)) register_2 (.D(pc), .en(stall), .Q(pc_2), .clk(clk), .clr(and_1_out));
  Register #(.width(32)) register_3 (.D(NPC), .en(stall), .Q(NPC_2), .clk(clk), .clr(and_1_out));
  Register #(.width(32)) register_4 (.D(IR), .en(stall), .Q(IR_2), .clk(clk), .clr(and_1_out));
  and and_1 (and_1_out, register_1_q, PCclear);
endmodule

module ID_EX (
  input  [31:0] IR,
  input  [1:0] alusela,
  input  [1:0] aluselb,
  input  dmld,
  input  dmsel,
  input  dmstr,
  input  [3:0] aluop,
  input  [1:0] rfd2sel,
  input  [1:0] rfd1sel,
  input  [31:0] pc,
  input  [31:0] rfd1,
  input  [31:0] rfd2,
  input  [31:0] immext,
  input  clk,
  input  stall,
  input  in_16,
  output [31:0] IR_2,
  output [1:0] alusela_2,
  output [1:0] aluselb_2,
  output dmld_2,
  output dmsel_2,
  output dmstr_2,
  output [3:0] aluop_2,
  output [1:0] rfd2sel_2,
  output [1:0] rfd1sel_2,
  output [31:0] pc_2,
  output [31:0] rfd1_2,
  output [31:0] rfd2_2,
  output [31:0] immext_2
);

  wire and_1_out, not_1_out, register_2_q;

  Register #(.width(2)) register_1 (.D(aluselb), .en(not_1_out), .Q(aluselb_2), .clk(clk), .clr(and_1_out));
  Register #(.width(1)) register_2 (.D(stall), .Q(register_2_q), .clk(clk));  // open: en, clr
  Register #(.width(32)) register_3 (.D(IR), .en(not_1_out), .Q(IR_2), .clk(clk), .clr(and_1_out));
  Register #(.width(2)) register_4 (.D(alusela), .en(not_1_out), .Q(alusela_2), .clk(clk), .clr(and_1_out));
  Register #(.width(1)) register_5 (.D(dmld), .en(not_1_out), .Q(dmld_2), .clk(clk), .clr(and_1_out));
  Register #(.width(1)) register_6 (.D(dmsel), .en(not_1_out), .Q(dmsel_2), .clk(clk), .clr(and_1_out));
  Register #(.width(1)) register_7 (.D(dmstr), .Q(dmstr_2), .clk(clk), .clr(and_1_out));  // open: en
  Register #(.width(4)) register_8 (.D(aluop), .en(not_1_out), .Q(aluop_2), .clk(clk), .clr(and_1_out));
  Register #(.width(2)) register_9 (.D(rfd2sel), .en(not_1_out), .Q(rfd2sel_2), .clk(clk), .clr(and_1_out));
  Register #(.width(2)) register_10 (.D(rfd1sel), .en(not_1_out), .Q(rfd1sel_2), .clk(clk), .clr(and_1_out));
  Register #(.width(32)) shdmt (.D(pc), .en(not_1_out), .Q(pc_2), .clk(clk), .clr(and_1_out));
  Register #(.width(32)) u_rfd1 (.D(rfd1), .en(not_1_out), .Q(rfd1_2), .clk(clk), .clr(and_1_out));
  Register #(.width(32)) u_rfd2 (.D(rfd2), .en(not_1_out), .Q(rfd2_2), .clk(clk), .clr(and_1_out));
  Register #(.width(32)) u_immext (.D(immext), .en(not_1_out), .Q(immext_2), .clk(clk), .clr(and_1_out));
  not not_1 (not_1_out, in_16);
  and and_1 (and_1_out, register_2_q, stall);
endmodule

module EX_MEM (
  input  [31:0] npc,
  input  dmld,
  input  dmsel,
  input  dmstr,
  input  [31:0] aluout,
  input  [31:0] rfd1,
  input  [31:0] rfd2,
  input  [31:0] pc,
  input  [31:0] IR,
  input  clk,
  input  rst,
  output [31:0] npc_2,
  output dmld_2,
  output dmsel_2,
  output dmstr_2,
  output [31:0] aluout_2,
  output [31:0] rfd1_2,
  output [31:0] rfd2_2,
  output [31:0] pc_2,
  output [31:0] IR_2
);

  wire undriven;

  Register #(.width(32)) u_npc (.D(npc), .Q(npc_2), .clk(clk), .clr(undriven));  // open: en
  Register #(.width(1)) register_1 (.D(dmld), .Q(dmld_2), .clk(clk), .clr(undriven));  // open: en
  Register #(.width(1)) register_2 (.D(dmsel), .Q(dmsel_2), .clk(clk), .clr(undriven));  // open: en
  Register #(.width(1)) register_3 (.D(dmstr), .Q(dmstr_2), .clk(clk), .clr(undriven));  // open: en
  Register #(.width(32)) register_4 (.D(aluout), .Q(aluout_2), .clk(clk), .clr(undriven));  // open: en
  Register #(.width(32)) u_rfd1 (.D(rfd1), .Q(rfd1_2), .clk(clk), .clr(undriven));  // open: en
  Register #(.width(32)) u_rfd2 (.D(rfd2), .Q(rfd2_2), .clk(clk), .clr(undriven));  // open: en
  Register #(.width(32)) u_pc (.D(pc), .Q(pc_2), .clk(clk), .clr(undriven));  // open: en
  Register #(.width(32)) u_pc_2 (.D(IR), .Q(IR_2), .clk(clk), .clr(undriven));  // open: en
endmodule

module MEM_WB (
  input  [31:0] pc,
  input  [31:0] dmdout,
  input  [31:0] aluout,
  input  [31:0] IR,
  input  [1:0] SEL,
  input  clk,
  input  rst,
  input  [31:0] rfd1,
  input  [31:0] rfd2,
  output [31:0] pc_2,
  output [31:0] dmdout_2,
  output [31:0] aluout_2,
  output [31:0] IR_2,
  output [1:0] SEL_2,
  output [31:0] rfd1_2,
  output [31:0] rfd2_2
);

  Register #(.width(32)) u_pc (.D(pc), .Q(pc_2), .clk(clk), .clr(rst));  // open: en
  Register #(.width(32)) register_1 (.D(dmdout), .Q(dmdout_2), .clk(clk), .clr(rst));  // open: en
  Register #(.width(32)) u_aluout (.D(aluout), .Q(aluout_2), .clk(clk), .clr(rst));  // open: en
  Register #(.width(32)) u_aluout_2 (.D(IR), .Q(IR_2), .clk(clk), .clr(rst));  // open: en
  Register #(.width(2)) register_2 (.D(SEL), .Q(SEL_2), .clk(clk), .clr(rst));  // open: en
  Register #(.width(32)) u_rfd1 (.D(rfd1), .Q(rfd1_2), .clk(clk), .clr(rst));  // open: en
  Register #(.width(32)) u_rfd2 (.D(rfd2), .Q(rfd2_2), .clk(clk), .clr(rst));  // open: en
endmodule

// src1mem
module ConfliJudge (
  input  [4:0] IDrt,
  input  [5:0] IDop,
  input  [5:0] IDfunct,
  input  [4:0] IDrs,
  input  [5:0] EXop,
  input  [5:0] EXfunct,
  input  [5:0] Memop,
  input  [5:0] Memfunct,
  input  [4:0] EXrd,
  input  [4:0] EXrt,
  input  [4:0] Memrd,
  input  [4:0] Memrt,
  output memaeq,
  output membeq,
  output stall,
  output aluaeq,
  output alubeq,
  output rfd2alueq,
  output rfd2dmeq,
  output src1ex,
  output src1mem
);

  wire and_1_out, and_2_out, and_3_out, and_4_out, and_5_out, and_8_out, and_9_out, and_11_out, and_12_out,
       and_13_out, and_16_out, and_17_out, and_20_out, comparator_1_eq, comparator_2_eq, comparator_3_eq,
       comparator_4_eq, comparator_5_eq, comparator_6_eq, comparator_7_eq, comparator_8_eq, comparator_9_eq,
       comparator_10_eq, comparator_11_eq, comparator_12_eq, comparator_13_eq, comparator_14_eq,
       comparator_15_eq, comparator_16_eq, comparator_17_eq, comparator_18_eq, comparator_19_eq,
       comparator_20_eq, comparator_21_eq, comparator_22_eq, comparator_23_eq, comparator_24_eq,
       comparator_25_eq, comparator_26_eq, comparator_27_eq, comparator_28_eq, comparator_29_eq,
       comparator_30_eq, comparator_31_eq, comparator_32_eq, comparator_33_eq, comparator_34_eq,
       comparator_35_eq, comparator_36_eq, comparator_37_eq, comparator_38_eq, comparator_39_eq,
       comparator_40_eq, comparator_41_eq, comparator_42_eq, comparator_43_eq, comparator_44_eq,
       comparator_45_eq, comparator_46_eq, comparator_47_eq, comparator_48_eq, comparator_49_eq,
       comparator_50_eq, comparator_51_eq, comparator_52_eq, comparator_53_eq, comparator_54_eq,
       comparator_55_eq, comparator_56_eq, comparator_57_eq, comparator_58_eq, comparator_59_eq,
       comparator_60_eq, comparator_61_eq, comparator_62_eq, comparator_63_eq, comparator_64_eq,
       comparator_65_eq, comparator_66_eq, comparator_67_eq, comparator_68_eq, comparator_69_eq,
       comparator_70_eq, comparator_71_eq, comparator_72_eq, comparator_73_eq, comparator_74_eq,
       comparator_75_eq, comparator_76_eq, comparator_77_eq, comparator_78_eq, comparator_79_eq,
       comparator_80_eq, comparator_81_eq, comparator_82_eq, comparator_83_eq, comparator_84_eq,
       comparator_85_eq, comparator_86_eq, comparator_87_eq, comparator_88_eq, comparator_89_eq,
       comparator_90_eq, comparator_91_eq, comparator_92_eq, comparator_93_eq, comparator_94_eq,
       comparator_95_eq, comparator_96_eq, comparator_97_eq, comparator_98_eq, comparator_99_eq,
       comparator_100_eq, comparator_101_eq, comparator_102_eq, comparator_103_eq, comparator_104_eq,
       comparator_105_eq, comparator_106_eq, comparator_107_eq, comparator_108_eq, comparator_109_eq,
       comparator_110_eq, comparator_111_eq, comparator_112_eq, comparator_113_eq, comparator_114_eq,
       comparator_115_eq, comparator_116_eq, comparator_117_eq, comparator_118_eq, comparator_119_eq,
       comparator_120_eq, comparator_121_eq, comparator_122_eq, comparator_123_eq, comparator_124_eq,
       comparator_127_eq, comparator_128_eq, comparator_129_eq, comparator_130_eq, comparator_131_eq,
       not_1_out, not_2_out, not_3_out, not_4_out, not_5_out, not_6_out, not_7_out, not_8_out, not_9_out,
       not_10_out, not_11_out, or_1_out, or_2_out, or_3_out, or_4_out, or_5_out, or_6_out, or_7_out,
       or_9_out, or_10_out, or_11_out, or_12_out, or_13_out, or_14_out, or_15_out, or_16_out, or_17_out,
       or_19_out, or_21_out, or_22_out, or_23_out, or_24_out, or_25_out, or_27_out;
  wire [1:0] and_6_out, and_21_out;
  wire [4:0] ALUA, ALUB, EXdt, IDsrc1, IDsrc2, lwdt, lwdt2, Memdt, multiplexer_1_out, multiplexer_2_out,
       multiplexer_5_out, multiplexer_6_out, multiplexer_8_out, multiplexer_13_out, multiplexer_14_out;

  Comparator #(.width(6)) comparator_1 (.a(6'b000010), .b(IDop), .eq(comparator_1_eq));  // open: gt, lt
  Comparator #(.width(6)) comparator_2 (.a(6'b000011), .b(IDop), .eq(comparator_2_eq));  // open: gt, lt
  Comparator #(.width(6)) comparator_3 (.a({6{1'b0}}), .b(IDop), .eq(comparator_3_eq));  // open: gt, lt
  Comparator #(.width(6)) comparator_4 (.a(IDfunct), .b({6{1'b0}}), .eq(comparator_4_eq));  // open: gt, lt
  Comparator #(.width(6)) comparator_5 (.a(IDfunct), .b(6'b000011), .eq(comparator_5_eq));  // open: gt, lt
  Comparator #(.width(6)) comparator_6 (.a(IDfunct), .b(6'b000010), .eq(comparator_6_eq));  // open: gt, lt
  Comparator #(.width(6)) comparator_7 (.a(IDfunct), .b(6'b001100), .eq(comparator_7_eq));  // open: gt, lt
  Comparator #(.width(6)) comparator_8 (.a(EXop), .b({6{1'b0}}), .eq(comparator_8_eq));  // open: gt, lt
  Comparator #(.width(6)) comparator_9 (.a(EXfunct), .b(6'b100000), .eq(comparator_9_eq));  // open: gt, lt
  Comparator #(.width(6)) comparator_10 (.a(EXfunct), .b(6'b100001), .eq(comparator_10_eq));  // open: gt, lt
  Comparator #(.width(6)) comparator_11 (.a(EXfunct), .b(6'b100100), .eq(comparator_11_eq));  // open: gt, lt
  Comparator #(.width(6)) comparator_12 (.a(EXfunct), .b({6{1'b0}}), .eq(comparator_12_eq));  // open: gt, lt
  Comparator #(.width(6)) comparator_13 (.a(EXfunct), .b(6'b000010), .eq(comparator_13_eq));  // open: gt, lt
  Comparator #(.width(6)) comparator_14 (.a(EXfunct), .b(6'b000011), .eq(comparator_14_eq));  // open: gt, lt
  Comparator #(.width(6)) comparator_15 (.a(EXfunct), .b(6'b100010), .eq(comparator_15_eq));  // open: gt, lt
  Comparator #(.width(6)) comparator_16 (.a(EXfunct), .b(6'b100101), .eq(comparator_16_eq));  // open: gt, lt
  Comparator #(.width(6)) comparator_17 (.a(EXfunct), .b(6'b100111), .eq(comparator_17_eq));  // open: gt, lt
  Comparator #(.width(6)) comparator_18 (.a(EXfunct), .b(6'b101010), .eq(comparator_18_eq));  // open: gt, lt
  Comparator #(.width(6)) comparator_19 (.a(EXfunct), .b(6'b101011), .eq(comparator_19_eq));  // open: gt, lt
  Comparator #(.width(6)) comparator_20 (.a(EXop), .b(6'b001000), .eq(comparator_20_eq));  // open: gt, lt
  Comparator #(.width(6)) comparator_21 (.a(EXop), .b(6'b001001), .eq(comparator_21_eq));  // open: gt, lt
  Comparator #(.width(6)) comparator_22 (.a(EXop), .b(6'b001100), .eq(comparator_22_eq));  // open: gt, lt
  Comparator #(.width(6)) comparator_23 (.a(EXop), .b(6'b001101), .eq(comparator_23_eq));  // open: gt, lt
  Comparator #(.width(6)) comparator_24 (.a(EXop), .b(6'b100011), .eq(comparator_24_eq));  // open: gt, lt
  Comparator #(.width(6)) comparator_25 (.a(EXop), .b(6'b001010), .eq(comparator_25_eq));  // open: gt, lt
  Comparator #(.width(6)) comparator_26 (.a(EXop), .b(6'b001110), .eq(comparator_26_eq));  // open: gt, lt
  Comparator #(.width(6)) comparator_27 (.a(EXop), .b(6'b100100), .eq(comparator_27_eq));  // open: gt, lt
  Comparator #(.width(6)) comparator_28 (.a(EXop), .b({6{1'b0}}), .eq(comparator_28_eq));  // open: gt, lt
  Comparator #(.width(6)) comparator_29 (.a(EXfunct), .b(6'b001000), .eq(comparator_29_eq));  // open: gt, lt
  Comparator #(.width(6)) comparator_30 (.a(EXfunct), .b(6'b001100), .eq(comparator_30_eq));  // open: gt, lt
  Comparator #(.width(6)) comparator_31 (.a(EXop), .b(6'b000100), .eq(comparator_31_eq));  // open: gt, lt
  Comparator #(.width(6)) comparator_32 (.a(EXop), .b(6'b000101), .eq(comparator_32_eq));  // open: gt, lt
  Comparator #(.width(6)) comparator_33 (.a(EXop), .b(6'b000010), .eq(comparator_33_eq));  // open: gt, lt
  Comparator #(.width(6)) comparator_34 (.a(EXop), .b(6'b000001), .eq(comparator_34_eq));  // open: gt, lt
  Comparator #(.width(6)) comparator_35 (.a(EXop), .b(6'b101011), .eq(comparator_35_eq));  // open: gt, lt
  Comparator #(.width(6)) comparator_36 (.a(IDop), .b({6{1'b0}}), .eq(comparator_36_eq));  // open: gt, lt
  Comparator #(.width(6)) comparator_37 (.a(IDfunct), .b({6{1'b0}}), .eq(comparator_37_eq));  // open: gt, lt
  Comparator #(.width(6)) comparator_38 (.a(IDfunct), .b(6'b000010), .eq(comparator_38_eq));  // open: gt, lt
  Comparator #(.width(6)) comparator_39 (.a(IDfunct), .b(6'b000011), .eq(comparator_39_eq));  // open: gt, lt
  Comparator #(.width(6)) comparator_40 (.a(IDfunct), .b(6'b000110), .eq(comparator_40_eq));  // open: gt, lt
  Comparator #(.width(6)) comparator_41 (.a(IDop), .b({6{1'b0}}), .eq(comparator_41_eq));  // open: gt, lt
  Comparator #(.width(6)) comparator_42 (.a(IDfunct), .b(6'b001000), .eq(comparator_42_eq));  // open: gt, lt
  Comparator #(.width(6)) comparator_43 (.a(IDfunct), .b(6'b001100), .eq(comparator_43_eq));  // open: gt, lt
  Comparator #(.width(6)) comparator_44 (.a(IDop), .b(6'b000001), .eq(comparator_44_eq));  // open: gt, lt
  Comparator #(.width(6)) comparator_45 (.a(IDop), .b(6'b000010), .eq(comparator_45_eq));  // open: gt, lt
  Comparator #(.width(6)) comparator_46 (.a(IDop), .b(6'b000011), .eq(comparator_46_eq));  // open: gt, lt
  Comparator #(.width(6)) comparator_47 (.a(EXfunct), .b(6'b000110), .eq(comparator_47_eq));  // open: gt, lt
  or or_1 (or_1_out, comparator_29_eq, comparator_30_eq, 1'b0);
  or or_2 (or_2_out, comparator_31_eq, comparator_32_eq, comparator_35_eq, comparator_33_eq, comparator_34_eq);
  or or_3 (or_3_out, comparator_37_eq, comparator_38_eq, comparator_39_eq, comparator_40_eq);
  or or_4 (or_4_out, 1'b0, comparator_42_eq, comparator_43_eq);
  or or_5 (or_5_out, comparator_44_eq, comparator_45_eq, comparator_46_eq);
  and and_1 (and_1_out, comparator_3_eq, or_6_out);
  or or_6 (or_6_out, comparator_4_eq, comparator_5_eq, comparator_6_eq);
  and and_2 (and_2_out, comparator_3_eq, comparator_7_eq);
  or or_7 (or_7_out, comparator_9_eq, comparator_14_eq, comparator_10_eq, comparator_11_eq, comparator_12_eq, comparator_13_eq, comparator_15_eq, comparator_16_eq, comparator_17_eq, comparator_18_eq, comparator_19_eq, comparator_47_eq);
  or or_8 (and_6_out[1], comparator_20_eq, comparator_26_eq, comparator_21_eq, comparator_22_eq, comparator_23_eq, comparator_24_eq, 1'b0, comparator_25_eq, comparator_27_eq);
  and and_3 (and_3_out, comparator_28_eq, or_1_out);
  and and_4 (and_4_out, comparator_36_eq, or_3_out);
  and and_5 (and_5_out, comparator_41_eq, or_4_out);
  or or_9 (or_9_out, comparator_1_eq, comparator_2_eq);
  and and_6 (and_6_out[0], comparator_8_eq, or_7_out);
  or or_10 (or_10_out, and_3_out, or_2_out);
  not not_1 (not_1_out, and_4_out);
  or or_11 (or_11_out, and_5_out, or_5_out);
  or or_12 (or_12_out, or_9_out, and_1_out);
  Multiplexer #(.width(5)) multiplexer_1 (
    .in0(IDrs), .in1(5'b00010), .out(multiplexer_1_out), .sel(and_2_out));  // open: en
  Multiplexer #(.width(5)) multiplexer_2 (
    .in0(IDrt), .in1(IDrs), .out(multiplexer_2_out), .sel(not_1_out));  // open: en
  Multiplexer #(.width(5)) multiplexer_3 (
    .in0(multiplexer_2_out), .in1({5{1'b0}}), .out(ALUA), .sel(or_11_out));  // open: en
  Multiplexer #(.width(5)) multiplexer_4 (
    .in0(multiplexer_1_out), .in1({5{1'b0}}), .out(IDsrc1), .sel(or_12_out));  // open: en
  Multiplexer #(.select(2), .width(5)) multiplexer_5 (
    .in0({5{1'b0}}), .in1(EXrd), .in2(EXrt), .in3({5{1'b0}}), .out(multiplexer_5_out), .sel(and_6_out));  // open: en
  Multiplexer #(.width(5)) multiplexer_6 (
    .in0(multiplexer_5_out), .in1({5{1'b0}}), .out(multiplexer_6_out), .sel(or_10_out));  // open: en
  Multiplexer #(.width(5)) multiplexer_7 (
    .in0(multiplexer_6_out), .in1({5{1'b1}}), .out(EXdt), .sel(comparator_48_eq));  // open: en
  Comparator #(.width(6)) comparator_48 (.a(EXop), .b(6'b000011), .eq(comparator_48_eq));  // open: gt, lt
  Comparator #(.width(5)) comparator_49 (.a(IDsrc1), .b(EXdt), .eq(comparator_49_eq));  // open: gt, lt
  Comparator #(.width(5)) comparator_50 (.a(Memdt), .b(IDsrc1), .eq(comparator_50_eq));  // open: gt, lt
  not not_2 (not_2_out, comparator_51_eq);
  Comparator #(.width(5)) comparator_51 (.a(IDsrc1), .b({5{1'b0}}), .eq(comparator_51_eq));  // open: gt, lt
  not not_3 (not_3_out, comparator_52_eq);
  Comparator #(.width(5)) comparator_52 (.a({5{1'b0}}), .b(IDsrc1), .eq(comparator_52_eq));  // open: gt, lt
  Comparator #(.width(6)) comparator_53 (.a(IDop), .b({6{1'b0}}), .eq(comparator_53_eq));  // open: gt, lt
  Comparator #(.width(6)) comparator_54 (.a(IDfunct), .b(6'b100000), .eq(comparator_54_eq));  // open: gt, lt
  Comparator #(.width(6)) comparator_55 (.a(IDfunct), .b(6'b100001), .eq(comparator_55_eq));  // open: gt, lt
  Comparator #(.width(6)) comparator_56 (.a(IDfunct), .b(6'b100100), .eq(comparator_56_eq));  // open: gt, lt
  Comparator #(.width(6)) comparator_57 (.a(IDfunct), .b(6'b100010), .eq(comparator_57_eq));  // open: gt, lt
  Comparator #(.width(6)) comparator_58 (.a(IDfunct), .b(6'b100101), .eq(comparator_58_eq));  // open: gt, lt
  Comparator #(.width(6)) comparator_59 (.a(IDfunct), .b(6'b100111), .eq(comparator_59_eq));  // open: gt, lt
  Comparator #(.width(6)) comparator_60 (.a(IDfunct), .b(6'b101010), .eq(comparator_60_eq));  // open: gt, lt
  Comparator #(.width(6)) comparator_61 (.a(IDfunct), .b(6'b101011), .eq(comparator_61_eq));  // open: gt, lt
  Comparator #(.width(6)) comparator_62 (.a({6{1'b0}}), .b(IDop), .eq(comparator_62_eq));  // open: gt, lt
  Comparator #(.width(6)) comparator_63 (.a(IDfunct), .b(6'b001000), .eq(comparator_63_eq));  // open: gt, lt
  Comparator #(.width(6)) comparator_64 (.a(IDop), .b(6'b001100), .eq(comparator_64_eq));  // open: gt, lt
  Comparator #(.width(6)) comparator_65 (.a(6'b001000), .b(IDop), .eq(comparator_65_eq));  // open: gt, lt
  Comparator #(.width(6)) comparator_66 (.a(6'b001001), .b(IDop), .eq(comparator_66_eq));  // open: gt, lt
  Comparator #(.width(6)) comparator_67 (.a(6'b001100), .b(IDop), .eq(comparator_67_eq));  // open: gt, lt
  Comparator #(.width(6)) comparator_68 (.a(6'b001101), .b(IDop), .eq(comparator_68_eq));  // open: gt, lt
  Comparator #(.width(6)) comparator_69 (.a(6'b100011), .b(IDop), .eq(comparator_69_eq));  // open: gt, lt
  Comparator #(.width(6)) comparator_70 (.a(IDop), .b(6'b001010), .eq(comparator_70_eq));  // open: gt, lt
  Comparator #(.width(6)) comparator_71 (.a(IDop), .b(6'b000010), .eq(comparator_71_eq));  // open: gt, lt
  Comparator #(.width(6)) comparator_72 (.a(IDop), .b(6'b000011), .eq(comparator_72_eq));  // open: gt, lt
  Comparator #(.width(6)) comparator_73 (.a(IDop), .b(6'b001110), .eq(comparator_73_eq));  // open: gt, lt
  Comparator #(.width(6)) comparator_74 (.a(IDop), .b(6'b100100), .eq(comparator_74_eq));  // open: gt, lt
  Comparator #(.width(6)) comparator_75 (.a(IDop), .b(6'b000001), .eq(comparator_75_eq));  // open: gt, lt
  Comparator #(.width(5)) comparator_76 (.a(IDsrc1), .b(lwdt), .eq(comparator_76_eq));  // open: gt, lt
  Comparator #(.width(5)) comparator_77 (.a(IDsrc1), .b(lwdt2), .eq(comparator_77_eq));  // open: gt, lt
  Comparator #(.width(5)) comparator_78 (.a(lwdt2), .b(IDsrc2), .eq(comparator_78_eq));  // open: gt, lt
  Comparator #(.width(5)) comparator_79 (.a(lwdt), .b(IDsrc2), .eq(comparator_79_eq));  // open: gt, lt
  Comparator #(.width(5)) comparator_80 (.a({5{1'b0}}), .b(EXdt), .eq(comparator_80_eq));  // open: gt, lt
  Comparator #(.width(5)) comparator_81 (.a(EXdt), .b(ALUA), .eq(comparator_81_eq));  // open: gt, lt
  Comparator #(.width(5)) comparator_82 (.a(EXdt), .b(IDsrc2), .eq(comparator_82_eq));  // open: gt, lt
  and and_7 (src1mem, comparator_50_eq, not_3_out);
  Comparator #(.width(6)) comparator_83 (.a(IDop), .b(6'b000100), .eq(comparator_83_eq));  // open: gt, lt
  Comparator #(.width(6)) comparator_84 (.a(IDop), .b(6'b000101), .eq(comparator_84_eq));  // open: gt, lt
  and and_8 (and_8_out, comparator_62_eq, comparator_63_eq);
  and and_9 (and_9_out, comparator_62_eq, comparator_64_eq);
  Comparator #(.width(5)) comparator_85 (.a(IDsrc1), .b({5{1'b0}}), .eq(comparator_85_eq));  // open: gt, lt
  not not_4 (not_4_out, comparator_85_eq);
  Comparator #(.width(5)) comparator_86 (.a({5{1'b0}}), .b(IDsrc2), .eq(comparator_86_eq));  // open: gt, lt
  not not_5 (not_5_out, comparator_80_eq);
  Comparator #(.width(5)) comparator_87 (.a(EXdt), .b(ALUB), .eq(comparator_87_eq));  // open: gt, lt
  Comparator #(.width(5)) comparator_88 (.a({5{1'b0}}), .b(ALUB), .eq(comparator_88_eq));  // open: gt, lt
  Comparator #(.width(5)) comparator_89 (.a({5{1'b0}}), .b(EXdt), .eq(comparator_89_eq));  // open: gt, lt
  Comparator #(.width(5)) comparator_90 (.a({5{1'b0}}), .b(Memdt), .eq(comparator_90_eq));  // open: gt, lt
  Comparator #(.width(5)) comparator_91 (.a(Memdt), .b(IDsrc2), .eq(comparator_91_eq));  // open: gt, lt
  and and_10 (src1ex, not_2_out, comparator_49_eq);
  and and_11 (and_11_out, comparator_53_eq, or_13_out);
  or or_13 (or_13_out, comparator_54_eq, comparator_55_eq, comparator_56_eq, comparator_57_eq, comparator_58_eq, comparator_59_eq, comparator_60_eq, comparator_61_eq);
  or or_14 (or_14_out, comparator_83_eq, comparator_84_eq);
  or or_15 (or_15_out, comparator_65_eq, comparator_66_eq, comparator_67_eq, comparator_68_eq, comparator_69_eq, 1'b0, comparator_70_eq, comparator_71_eq, comparator_72_eq, comparator_73_eq, comparator_74_eq, comparator_75_eq);
  and and_12 (and_12_out, comparator_78_eq, not_6_out);
  and and_13 (and_13_out, comparator_79_eq, not_6_out);
  not not_6 (not_6_out, comparator_86_eq);
  and and_14 (aluaeq, not_5_out, comparator_81_eq);
  not not_7 (not_7_out, comparator_88_eq);
  not not_8 (not_8_out, comparator_89_eq);
  and and_15 (rfd2alueq, not_8_out, comparator_82_eq);
  not not_9 (not_9_out, comparator_90_eq);
  or or_16 (or_16_out, and_11_out, or_14_out);
  Multiplexer #(.width(5)) multiplexer_8 (
    .in0(IDrt), .in1(5'b00100), .out(multiplexer_8_out), .sel(and_9_out));  // open: en
  or or_17 (or_17_out, and_8_out, or_15_out);
  and and_16 (and_16_out, not_4_out, comparator_76_eq);
  and and_17 (and_17_out, not_4_out, comparator_77_eq);
  or or_18 (stall, and_16_out, and_17_out);
  or or_19 (or_19_out, and_12_out, and_13_out);
  and and_18 (alubeq, comparator_87_eq, not_7_out);
  and and_19 (rfd2dmeq, not_9_out, comparator_91_eq);
  Multiplexer #(.width(5)) multiplexer_9 (
    .in0(multiplexer_8_out), .in1({5{1'b0}}), .out(IDsrc2), .sel(or_17_out));  // open: en
  // OR_Gate or_20 has open pins: in0=stall, out=open
  Multiplexer #(.width(5)) multiplexer_10 (.in0({5{1'b0}}), .in1(IDrt), .out(ALUB), .sel(or_16_out));  // open: en
  Comparator #(.width(6)) comparator_92 (.a(6'b100100), .b(EXop), .eq(comparator_92_eq));  // open: gt, lt
  Comparator #(.width(6)) comparator_93 (.a(6'b100011), .b(EXop), .eq(comparator_93_eq));  // open: gt, lt
  Comparator #(.width(6)) comparator_94 (.a(Memop), .b({6{1'b0}}), .eq(comparator_94_eq));  // open: gt, lt
  Comparator #(.width(6)) comparator_95 (.a(Memfunct), .b(6'b100000), .eq(comparator_95_eq));  // open: gt, lt
  Comparator #(.width(6)) comparator_96 (.a(Memfunct), .b(6'b100001), .eq(comparator_96_eq));  // open: gt, lt
  Comparator #(.width(6)) comparator_97 (.a(Memfunct), .b(6'b100100), .eq(comparator_97_eq));  // open: gt, lt
  Comparator #(.width(6)) comparator_98 (.a(Memfunct), .b({6{1'b0}}), .eq(comparator_98_eq));  // open: gt, lt
  Comparator #(.width(6)) comparator_99 (.a(Memfunct), .b(6'b000010), .eq(comparator_99_eq));  // open: gt, lt
  Comparator #(.width(6)) comparator_100 (.a(Memfunct), .b(6'b000011), .eq(comparator_100_eq));  // open: gt, lt
  Comparator #(.width(6)) comparator_101 (.a(Memfunct), .b(6'b100010), .eq(comparator_101_eq));  // open: gt, lt
  Comparator #(.width(6)) comparator_102 (.a(Memfunct), .b(6'b100101), .eq(comparator_102_eq));  // open: gt, lt
  Comparator #(.width(6)) comparator_103 (.a(Memfunct), .b(6'b100111), .eq(comparator_103_eq));  // open: gt, lt
  Comparator #(.width(6)) comparator_104 (.a(Memfunct), .b(6'b101010), .eq(comparator_104_eq));  // open: gt, lt
  Comparator #(.width(6)) comparator_105 (.a(Memfunct), .b(6'b101011), .eq(comparator_105_eq));  // open: gt, lt
  Comparator #(.width(6)) comparator_106 (.a(Memop), .b(6'b001000), .eq(comparator_106_eq));  // open: gt, lt
  Comparator #(.width(6)) comparator_107 (.a(Memop), .b(6'b001001), .eq(comparator_107_eq));  // open: gt, lt
  Comparator #(.width(6)) comparator_108 (.a(Memop), .b(6'b001100), .eq(comparator_108_eq));  // open: gt, lt
  Comparator #(.width(6)) comparator_109 (.a(Memop), .b(6'b001101), .eq(comparator_109_eq));  // open: gt, lt
  Comparator #(.width(6)) comparator_110 (.a(Memop), .b(6'b100011), .eq(comparator_110_eq));  // open: gt, lt
  Comparator #(.width(6)) comparator_111 (.a(Memop), .b(6'b001010), .eq(comparator_111_eq));  // open: gt, lt
  Comparator #(.width(6)) comparator_112 (.a(Memop), .b(6'b001110), .eq(comparator_112_eq));  // open: gt, lt
  Comparator #(.width(6)) comparator_113 (.a(Memop), .b(6'b100100), .eq(comparator_113_eq));  // open: gt, lt
  Comparator #(.width(6)) comparator_114 (.a(Memop), .b({6{1'b0}}), .eq(comparator_114_eq));  // open: gt, lt
  Comparator #(.width(6)) comparator_115 (.a(Memfunct), .b(6'b001000), .eq(comparator_115_eq));  // open: gt, lt
  Comparator #(.width(6)) comparator_116 (.a(Memfunct), .b(6'b001100), .eq(comparator_116_eq));  // open: gt, lt
  Comparator #(.width(6)) comparator_117 (.a(Memfunct), .b(6'b000110), .eq(comparator_117_eq));  // open: gt, lt
  Comparator #(.width(6)) comparator_118 (.a(Memop), .b(6'b000100), .eq(comparator_118_eq));  // open: gt, lt
  Comparator #(.width(6)) comparator_119 (.a(Memop), .b(6'b000101), .eq(comparator_119_eq));  // open: gt, lt
  Comparator #(.width(6)) comparator_120 (.a(Memop), .b(6'b000010), .eq(comparator_120_eq));  // open: gt, lt
  Comparator #(.width(6)) comparator_121 (.a(Memop), .b(6'b000001), .eq(comparator_121_eq));  // open: gt, lt
  Comparator #(.width(6)) comparator_122 (.a(Memop), .b(6'b101011), .eq(comparator_122_eq));  // open: gt, lt
  or or_21 (or_21_out, comparator_92_eq, comparator_93_eq);
  Comparator #(.width(6)) comparator_123 (.a(6'b100011), .b(Memop), .eq(comparator_123_eq));  // open: gt, lt
  Comparator #(.width(6)) comparator_124 (.a(6'b100100), .b(Memop), .eq(comparator_124_eq));  // open: gt, lt
  or or_22 (or_22_out, comparator_115_eq, comparator_116_eq, comparator_117_eq);
  or or_23 (or_23_out, comparator_118_eq, comparator_119_eq, comparator_122_eq, comparator_120_eq, comparator_121_eq);
  or or_24 (or_24_out, comparator_123_eq, comparator_124_eq);
  Comparator #(.width(5)) comparator_125 ();  // open: a, b, gt, eq, lt
  Comparator #(.width(6)) comparator_126 (.a(6'b100011), .b(Memop));  // open: gt, eq, lt
  or or_25 (or_25_out, comparator_95_eq, comparator_96_eq, comparator_97_eq, comparator_98_eq, comparator_99_eq, comparator_100_eq, comparator_101_eq, comparator_102_eq, comparator_103_eq, comparator_104_eq, comparator_105_eq);
  or or_26 (and_21_out[1], comparator_106_eq, comparator_112_eq, comparator_107_eq, comparator_108_eq, comparator_109_eq, comparator_110_eq, 1'b0, comparator_111_eq, comparator_113_eq);
  and and_20 (and_20_out, comparator_114_eq, or_22_out);
  Multiplexer #(.width(5)) multiplexer_11 (.in0({5{1'b0}}), .in1(EXrt), .out(lwdt), .sel(or_21_out));  // open: en
  Multiplexer #(.width(5)) multiplexer_12 (.in0({5{1'b0}}), .in1(Memrt), .out(lwdt2), .sel(or_24_out));  // open: en
  Comparator #(.width(5)) comparator_127 (.a({5{1'b0}}), .b(Memdt), .eq(comparator_127_eq));  // open: gt, lt
  Comparator #(.width(5)) comparator_128 (.a(Memdt), .b(ALUA), .eq(comparator_128_eq));  // open: gt, lt
  Comparator #(.width(5)) comparator_129 (.a(Memdt), .b(ALUB), .eq(comparator_129_eq));  // open: gt, lt
  and and_21 (and_21_out[0], comparator_94_eq, or_25_out);
  not not_10 (not_10_out, comparator_127_eq);
  not not_11 (not_11_out, comparator_130_eq);
  Comparator #(.width(5)) comparator_130 (.a(Memdt), .b({5{1'b0}}), .eq(comparator_130_eq));  // open: gt, lt
  or or_27 (or_27_out, and_20_out, or_23_out);
  and u_Memaeq (memaeq, not_10_out, comparator_128_eq);
  and u_Membeq (membeq, comparator_129_eq, not_11_out);
  Multiplexer #(.select(2), .width(5)) multiplexer_13 (
    .in0({5{1'b0}}), .in1(Memrd), .in2(Memrt), .in3({5{1'b0}}), .out(multiplexer_13_out), .sel(and_21_out));  // open: en
  Multiplexer #(.width(5)) multiplexer_14 (
    .in0(multiplexer_13_out), .in1({5{1'b0}}), .out(multiplexer_14_out), .sel(or_27_out));  // open: en
  Multiplexer #(.width(5)) multiplexer_15 (
    .in0(multiplexer_14_out), .in1({5{1'b1}}), .out(Memdt), .sel(comparator_131_eq));  // open: en
  Comparator #(.width(6)) comparator_131 (.a(EXop), .b(6'b000011), .eq(comparator_131_eq));  // open: gt, lt

  // Notes on the sheet:
  //   空操作
endmodule

module parser (
  input  [31:0] IR,
  output [5:0] funct,
  output [4:0] shamt,
  output [4:0] rd,
  output [4:0] rt,
  output [4:0] rs,
  output [5:0] OP
);


  assign funct = IR[5:0];
  assign OP = IR[31:26];
  assign rd = IR[15:11];
  assign rs = IR[25:21];
  assign rt = IR[20:16];
  assign shamt = IR[10:6];
endmodule

module ALUSrcsel (
  input  idsrc1mem,
  input  idsrc1ex,
  input  memaeq,
  input  aluaeq,
  input  memebeq,
  input  alubeq,
  input  rfd2dmbeq,
  input  rfd2alueq,
  output [1:0] rfd1sel,
  output [1:0] sela,
  output [1:0] selb,
  output [1:0] rfd2sel
);

  wire comparator_1_eq, comparator_2_eq, comparator_3_eq, comparator_4_eq;

  Comparator #(.width(2)) comparator_1 (.a(2'b11), .b({idsrc1mem, idsrc1ex}), .eq(comparator_1_eq));  // open: gt, lt
  Comparator #(.width(2)) comparator_2 (.a(2'b11), .b({memaeq, aluaeq}), .eq(comparator_2_eq));  // open: gt, lt
  Comparator #(.width(2)) comparator_3 (.a(2'b11), .b({memebeq, alubeq}), .eq(comparator_3_eq));  // open: gt, lt
  Comparator #(.width(2)) comparator_4 (.a(2'b11), .b({rfd2dmbeq, rfd2alueq}), .eq(comparator_4_eq));  // open: gt, lt
  Multiplexer #(.width(2)) multiplexer_1 (
    .in0({idsrc1mem, idsrc1ex}), .in1(2'b01), .out(rfd1sel), .sel(comparator_1_eq));  // open: en
  Multiplexer #(.width(2)) multiplexer_2 (
    .in0({memaeq, aluaeq}), .in1(2'b01), .out(sela), .sel(comparator_2_eq));  // open: en
  Multiplexer #(.width(2)) multiplexer_3 (
    .in0({memebeq, alubeq}), .in1(2'b01), .out(selb), .sel(comparator_3_eq));  // open: en
  Multiplexer #(.width(2)) multiplexer_4 (
    .in0({rfd2dmbeq, rfd2alueq}), .in1(2'b01), .out(rfd2sel), .sel(comparator_4_eq));  // open: en
endmodule
