// Logisim project lab4 - int.circ as structural Verilog: 11 circuits, main circuit main
module main (
  input  in_1,
  output out_2,
  output out_3,
  output out_4,
  output [15:0] out_5
);

  wire \_1号中断 , \_1号中断_out , \_1号中断等待指示 , \_2号中断 , \_2号中断_out , \_2号中断等待指示 , \_3号中断 , \_3号中断_out ,
       \_3号中断等待指示 , alu_1_p8, alusrcb_1_alusrcb, and_1_out, and_2_out, and_3_out, and_4_out, and_5_out,
       and_6_out, and_7_out, and_8_out, and_9_out, and_10_out, and_11_out, and_12_out, and_13_out,
       and_14_out, and_16_out, clock_1_out, clock_2_out, clock_3_out, clock_4_out, clock_5_out, clock_6_out,
       clock_7_out, clock_8_out, clock_9_out, clock_10_out, clock_11_out, clock_12_out, comparator_1_eq,
       comparator_2_eq, comparator_3_eq, comparator_4_eq, comparator_5_eq, comparator_6_eq, comparator_7_eq,
       comparator_9_eq, comparator_10_eq, comparator_11_eq, comparator_12_eq, comparator_13_eq,
       comparator_14_eq, comparator_15_eq, comparator_16_eq, comparator_17_eq, comparator_18_eq,
       comparator_19_eq, comparator_20_eq, d_ff_1_q, d_ff_2_q, d_ff_3_q, d_ff_4_q, dmload_1_dmload,
       dmsel_1_dmsel, EPC_2_q, EPC_4_q, EPC_q, epcen, erettsig, IE_2_q, intin, IR1_q, not_1_out, not_2_out,
       not_3_out, not_5_out, or_2_out, or_3_out, or_4_out, or_6_out, or_7_out, or_8_out, or_9_out, PCen,
       register_4_q, register_5_q, register_6_q, rfw_1_alusrcb, RST;
  wire [1:1] register_2_q;
  wire [2:0] and_15_out, multiplexer_5_out, or_5_out, priority_encoder_1_out, \当前中断 ;
  wire [3:0] aluop_1_out_3, register_7_q_2, register_7_q_3, register_7_q_4, register_7_q_5, register_7_q_6,
       register_7_q_7;
  wire [4:0] multiplexer_2_out, multiplexer_4_out, registerfile_1_p6, registerfile_1_p7, rs, rt;
  wire [5:0] funct, OP;
  wire [11:0] register_7_q;
  wire [15:0] counter_3_q, counter_4_q, counter_5_q;
  wire [15:6] imm;
  wire [31:0] alu_1_p2, Aluout, dmdout, EPC, epc_t, extcuit_1_out_4, intpc, multiplexer_1_out,
       multiplexer_3_out, multiplexer_6_out, multiplexer_7_out, pc, pccuit_1_newpc, rfd1, rfd2, rfdin_1_out_6;

  Comparator #(.width(32)) comparator_1 (.a(intpc), .b({32{1'b0}}), .eq(comparator_1_eq));  // open: gt, lt
  Register #(.width(32)) register_1 (.D(pccuit_1_newpc), .Q(epc_t), .clk(clock_1_out));  // open: en, clr
  Clock clock_1 (.out(clock_1_out));
  not not_1 (not_1_out, comparator_1_eq);
  Comparator #(.width(32)) comparator_2 (.a(intpc), .b(pc), .eq(comparator_2_eq));  // open: gt, lt
  Register #(.width(1)) register_2 (.D(1'b1), .Q(register_2_q[1]), .clk(intin), .clr(and_1_out));  // open: en
  and and_1 (and_1_out, comparator_2_eq, not_1_out);
  // Probe on OP
  Multiplexer #(.select(2), .width(32)) multiplexer_1 (
    .in0(pccuit_1_newpc), .in1(EPC), .in2(intpc), .out(multiplexer_1_out), .sel({register_2_q[1], erettsig}));  // open: in3, en
  // Probe on rs
  // Probe on {imm, funct}
  Register #(.width(32)) register_3 (.D(multiplexer_1_out), .en(PCen), .Q(pc), .clk(clock_2_out), .clr(RST));
  Clock clock_2 (.out(clock_2_out));
  Comparator #(.width(6)) comparator_3 (.a(OP), .b(6'b000011), .eq(comparator_3_eq));  // open: gt, lt
  Button button_1 (.out(RST));
  Counter #(.width(16), .max('hffff)) counter_1 (
    .load(RST), .D({16{1'b0}}), .count(PCen), .Q(out_5), .clk(clock_2_out), .clr(RST));  // open: carry
  // Probe on rt
  pccuit pccuit_1 (
    .op(OP), .pc(pc), .Aluout(Aluout), .label({rs, rt, imm, funct}), .rfd1(rfd1), .funct(funct),
    .newpc(pccuit_1_newpc), .clk(clock_2_out), .pcen(PCen));
  Multiplexer #(.width(5)) multiplexer_2 (
    .in0(multiplexer_4_out), .in1({5{1'b1}}), .out(multiplexer_2_out), .sel(comparator_3_eq));  // open: en
  // Probe on out_5
  // Probe on imm[10:6]
  // Probe on imm[15:11]
  Clock clock_3 (.out(clock_3_out));
  Button \u__1号中断  (.out(\_1号中断_out ));
  LED \_1号中断等待指示灯  (.in(or_2_out));
  Clock clock_4 (.out(clock_4_out));
  Button \u__2号中断  (.out(\_2号中断_out ));
  LED \_1号中断等待指示灯_2  (.in(or_3_out));
  Clock clock_5 (.out(clock_5_out));
  Button \u__3号中断  (.out(\_3号中断_out ));
  LED \_1号中断等待指示灯_3  (.in(or_4_out));
  or or_1 (epcen, or_2_out, or_3_out, or_4_out);
  // Probe on funct
  ROM #(.addrWidth(24), .dataWidth(32)) rom_1 (.addr({2'b00, pc[23:2]}), .data({OP, rs, rt, imm, funct}));  // open: sel
  Comparator #(.width(6)) comparator_4 (.a(OP), .b(6'b001111), .eq(comparator_4_eq));  // open: gt, lt
  or or_2 (or_2_out, IR1_q, d_ff_1_q);
  or or_3 (or_3_out, or_5_out[1], d_ff_2_q);
  or or_4 (or_4_out, or_5_out[2], d_ff_3_q);
  // Probe on {rs, rt, imm, funct}
  Multiplexer #(.width(32)) multiplexer_3 (
    .in0(rfdin_1_out_6), .in1({imm, funct, {16{1'b0}}}), .out(multiplexer_3_out), .sel(comparator_4_eq));  // open: en
  D_Flip_Flop d_ff_1 (.clk(\_1号中断_out ), .D(1'b1), .Q(d_ff_1_q), .reset(IR1_q));  // open: Qn, preset, en
  D_Flip_Flop d_ff_2 (.clk(\_2号中断_out ), .D(1'b1), .Q(d_ff_2_q), .reset(or_5_out[1]));  // open: Qn, preset, en
  D_Flip_Flop d_ff_3 (.clk(\_3号中断_out ), .D(1'b1), .Q(d_ff_3_q), .reset(or_5_out[2]));  // open: Qn, preset, en
  Multiplexer #(.width(5)) multiplexer_4 (
    .in0(rt), .in1(imm[15:11]), .out(multiplexer_4_out), .sel(comparator_5_eq));  // open: en
  Extcuit extcuit_1 (.in_1({imm, funct}), .in_2(OP), .in_3(funct), .out_4(extcuit_1_out_4));
  or or_5 (or_5_out[0], d_ff_1_q, IR1_q);
  and and_2 (and_2_out, or_5_out[0], ~and_3_out);  // AND_Gate
  and and_3 (and_3_out, erettsig, \当前中断 [0]);
  or or_6 (or_6_out, d_ff_2_q, or_5_out[1]);
  and and_4 (and_4_out, or_6_out, ~and_6_out);  // AND_Gate
  or or_7 (or_7_out, d_ff_3_q, or_5_out[2]);
  and and_5 (and_5_out, or_7_out, ~and_7_out);  // AND_Gate
  Clock clock_6 (.out(clock_6_out));
  Register #(.width(1)) register_4 (.D(intin), .Q(register_4_q), .clk(clock_7_out));  // open: en, clr
  Clock clock_7 (.out(clock_7_out));
  Rfdin rfdin_1 (.op(OP), .funct(funct), .dmout(dmdout), .Aluout(Aluout), .pc(pc), .out_6(rfdin_1_out_6));
  Rfw rfw_1 (.op(OP), .funct(funct), .AlusrcB(rfw_1_alusrcb));
  Comparator #(.width(6)) comparator_5 (.a({6{1'b0}}), .b(OP), .eq(comparator_5_eq));  // open: gt, lt
  Comparator #(.width(1)) comparator_6 (.a(and_10_out), .b(1'b1), .eq(comparator_6_eq));  // open: gt, lt
  Comparator #(.width(32)) comparator_7 (.a(rfd1), .b(32'h1), .eq(comparator_7_eq));  // open: gt, lt
  D_Flip_Flop IR1 (.clk(clock_3_out), .D(and_2_out), .Q(IR1_q));  // open: Qn, preset, en, reset
  D_Flip_Flop IR1_2 (.clk(clock_4_out), .D(and_4_out), .Q(or_5_out[1]));  // open: Qn, preset, en, reset
  and and_6 (and_6_out, erettsig, \当前中断 [1]);
  and and_7 (and_7_out, erettsig, \当前中断 [2]);
  not not_2 (not_2_out, d_ff_4_q);
  Register #(.width(1)) register_5 (.D(erettsig), .Q(register_5_q), .clk(clock_6_out));  // open: en, clr
  Register #(.width(1)) register_6 (.D(register_4_q), .Q(register_6_q), .clk(clock_7_out));  // open: en, clr
  Comparator #(.width(6)) comparator_8 (.a(OP), .b(6'b010000), .eq(erettsig));  // open: gt, lt
  not not_3 (not_3_out, comparator_7_eq);
  D_Flip_Flop IR1_3 (.clk(clock_5_out), .D(and_5_out), .Q(or_5_out[2]));  // open: Qn, preset, en, reset
  D_Flip_Flop d_ff_4 (.clk(or_8_out), .D(not_2_out), .Q(d_ff_4_q));  // open: Qn, preset, en, reset
  or or_8 (or_8_out, register_5_q, register_6_q);
  Comparator #(.width(6)) comparator_9 (.a(funct), .b({6{1'b0}}), .eq(comparator_9_eq));  // open: gt, lt
  Comparator #(.width(6)) comparator_10 (.a(funct), .b(6'b000010), .eq(comparator_10_eq));  // open: gt, lt
  Comparator #(.width(6)) comparator_11 (.a(funct), .b(6'b000011), .eq(comparator_11_eq));  // open: gt, lt
  Comparator #(.width(6)) comparator_12 (.a(funct), .b(6'b000110), .eq(comparator_12_eq));  // open: gt, lt
  Comparator #(.width(6)) comparator_13 (.a(OP), .b({6{1'b0}}), .eq(comparator_13_eq));  // open: gt, lt
  // RegisterFile registerfile_1: pin names not known; wires that end beside it: {rs, rt, imm, funct}, multiplexer_3_out, clock_2_out, rfw_1_alusrcb, multiplexer_2_out, registerfile_1_p6, registerfile_1_p7, rfd1, rfd2, rfd1
  Aluop aluop_1 (.funct(funct), .op(OP), .out_3(aluop_1_out_3));
  Comparator #(.width(6)) comparator_14 (.a(funct), .b(6'b001100), .eq(comparator_14_eq));  // open: gt, lt
  Comparator #(.width(6)) comparator_15 (.a(OP), .b({6{1'b0}}), .eq(comparator_15_eq));  // open: gt, lt
  Register #(.width(32)) register_7 (
    .D(rfd2), .en(and_8_out),
    .Q({register_7_q_7, register_7_q_6, register_7_q_5, register_7_q_4, register_7_q_3, register_7_q[11:8], register_7_q_2, register_7_q[3:0]}),
    .clk(clock_2_out), .clr(RST));
  and and_8 (and_8_out, comparator_6_eq, not_3_out);
  and and_9 (and_9_out, comparator_6_eq, comparator_7_eq);
  Multiplexer #(.width(3)) multiplexer_5 (
    .in0(3'b111), .in1(3'b000), .out(multiplexer_5_out), .sel(d_ff_4_q));  // open: en
  Register #(.width(1)) u_EPC (.D(epcen), .Q(EPC_q), .clk(clock_9_out));  // open: en, clr
  Clock clock_8 (.out(clock_8_out));
  Clock clock_9 (.out(clock_9_out));
  Multiplexer #(.width(32)) multiplexer_6 (
    .in0(rfd1), .in1(rfd2), .out(multiplexer_6_out), .sel(and_14_out));  // open: en
  Multiplexer #(.width(32)) multiplexer_7 (
    .in0(rfd2), .in1(extcuit_1_out_4), .out(multiplexer_7_out), .sel(alusrcb_1_alusrcb));  // open: en
  and and_10 (and_10_out, comparator_14_eq, comparator_15_eq);
  Hex_Digit_Display hex_digit_display_1 (.value(register_7_q_6));  // open: dp
  Hex_Digit_Display hex_digit_display_2 (.value(register_7_q_7));  // open: dp
  not not_4 (PCen, and_9_out);
  Button _1 (.out(\_1号中断 ));
  Button _2 (.out(\_2号中断 ));
  Button _3 (.out(\_3号中断 ));
  and and_11 (and_11_out, IR1_q, 1'b1);
  and and_12 (and_12_out, or_5_out[1], 1'b1);
  and and_13 (and_13_out, or_5_out[2], 1'b1);
  Clock clock_10 (.out(clock_10_out));
  not not_5 (not_5_out, EPC_2_q);
  Register #(.width(1)) EPC_2 (.D(EPC_q), .Q(EPC_2_q), .clk(clock_8_out));  // open: en, clr
  or or_9 (or_9_out, comparator_9_eq, comparator_10_eq, comparator_11_eq, comparator_12_eq);
  // ALU alu_1: pin names not known; wires that end beside it: multiplexer_6_out, alu_1_p2, out_2, aluop_1_out_3, out_3, out_4, Aluout, alu_1_p8, RST
  AlusrcB alusrcb_1 (.op(OP), .funct(funct), .AlusrcB(alusrcb_1_alusrcb));
  Multiplexer #(.width(5)) multiplexer_8 (
    .in0(rs), .in1(5'b00010), .out(registerfile_1_p6), .sel(and_10_out));  // open: en
  Multiplexer #(.width(5)) multiplexer_9 (
    .in0(rt), .in1(5'b00100), .out(registerfile_1_p7), .sel(and_10_out));  // open: en
  Hex_Digit_Display hex_digit_display_3 (.value(register_7_q_4));  // open: dp
  Hex_Digit_Display hex_digit_display_4 (.value(register_7_q_5));  // open: dp
  Priority_Encoder priority_encoder_1 (
    .in0(1'b1), .in1(and_11_out), .in2(and_12_out), .in4(and_13_out), .out(priority_encoder_1_out));  // open: in3, in5, in6, in7, en_in, gs, en_out
  Register #(.width(3)) IE (.D(3'b111), .clk(clock_10_out), .clr(IE_2_q));  // open: en, Q
  Register #(.width(1)) IE_2 (.D(1'b1), .Q(IE_2_q), .clr(in_1));  // open: en, clk
  Register #(.width(32)) EPC_3 (.D(epc_t), .en(not_5_out), .Q(EPC), .clk(intin));  // open: clr
  Comparator #(.width(6)) comparator_16 (.a(OP), .b({6{1'b0}}), .eq(comparator_16_eq));  // open: gt, lt
  Comparator #(.width(6)) comparator_17 (.a(funct), .b(6'b000110), .eq(comparator_17_eq));  // open: gt, lt
  Dmload dmload_1 (.op(OP), .Dmload(dmload_1_dmload));
  Dmsel dmsel_1 (.op(OP), .Dmsel(dmsel_1_dmsel));
  Dmstr dmstr_1 (.op(OP), .Dmsel(alu_1_p8));
  Hex_Digit_Display hex_digit_display_5 (.value(register_7_q_3));  // open: dp
  Hex_Digit_Display hex_digit_display_6 (.value(register_7_q[11:8]));  // open: dp
  LED _1_2 (.in(\_1号中断等待指示 ));
  LED _2_2 (.in(\_2号中断等待指示 ));
  LED _3_2 (.in(\_3号中断等待指示 ));
  // Probe on priority_encoder_1_out
  Counter counter_2 ();  // open: load, D, count, Q, carry, clk, clr
  Clock clock_11 (.out(clock_11_out));
  Register #(.width(1)) EPC_4 (.D(erettsig), .Q(EPC_4_q), .clk(clock_12_out));  // open: en, clr
  Clock clock_12 (.out(clock_12_out));
  and and_14 (and_14_out, or_9_out, comparator_13_eq);
  // Probe on Aluout
  Hex_Digit_Display hex_digit_display_7 (.value(register_7_q_2));  // open: dp
  Hex_Digit_Display hex_digit_display_8 (.value(register_7_q[3:0]));  // open: dp
  // Probe on intpc
  assign and_15_out = priority_encoder_1_out & multiplexer_5_out;  // AND_Gate and_15, 3 bits wide
  or or_10 (intin, and_15_out[2], and_15_out[1], and_15_out[0]);
  Counter #(.width(16), .max('hffff)) counter_3 (
    .count(and_15_out[2]), .Q(counter_3_q), .clk(clock_11_out), .clr(EPC_4_q));  // open: load, D, carry
  Comparator #(.width(16)) comparator_18 (.a(counter_3_q), .b({16{1'b0}}), .eq(comparator_18_eq));  // open: gt, lt
  and and_16 (and_16_out, comparator_16_eq, comparator_17_eq);
  Multiplexer #(.width(32)) multiplexer_10 (
    .in0(multiplexer_7_out), .in1(rfd1), .out(alu_1_p2), .sel(and_16_out));  // open: en
  RAM #(.addrWidth(24), .dataWidth(32), .bus("separate")) ram_1 (
    .addr(Aluout[23:0]), .din(rfd2), .data(dmdout), .str(dmload_1_dmload), .sel(dmsel_1_dmsel),
    .clk(clock_2_out));  // open: ld, clr
  Multiplexer #(.select(3), .width(32)) multiplexer_11 (
    .in0({32{1'b0}}), .in1(32'h28), .in2(32'hd8), .in4(32'h188), .in5({32{1'b0}}), .in6({32{1'b0}}),
    .in7({32{1'b0}}), .out(intpc), .sel(and_15_out));  // open: in3, en
  Counter #(.width(16), .max('hffff)) counter_4 (
    .count(and_15_out[1]), .Q(counter_4_q), .clk(clock_11_out), .clr(EPC_4_q));  // open: load, D, carry
  Comparator #(.width(16)) comparator_19 (.a(counter_4_q), .b({16{1'b0}}), .eq(comparator_19_eq));  // open: gt, lt
  not not_6 (\当前中断 [2], comparator_18_eq);
  // Probe on \当前中断 
  Counter #(.width(16), .max('hffff)) counter_5 (
    .count(and_15_out[0]), .Q(counter_5_q), .clk(clock_11_out), .clr(EPC_4_q));  // open: load, D, carry
  not not_7 (\当前中断 [1], comparator_19_eq);
  Comparator #(.width(16)) comparator_20 (.a(counter_5_q), .b({16{1'b0}}), .eq(comparator_20_eq));  // open: gt, lt
  not not_8 (\当前中断 [0], comparator_20_eq);

  // Other names for the same wires on the sheet: imm[5:0] = funct; shdmt[4:0] = imm[10:6]; rd[4:0] = imm[15:11]

  // Notes on the sheet:
  //         总复位
  //   contents of rom_1 (hex, n*v repeats v):
  //   20110200 20020022 112020 c 2231ffff 1620fffc 20020032 c 2002000a c 201d07d0 27bdfffc afb00000
  //   27bdfffc afb30000 27bdfffc afb40000 27bdfffc afb50000 27bdfffc afb60000 27bdfffc afa40000 27bdfffc
  //   afa20000 20160001 20140006 20150001 168020 108100 2149825 132020 20020022 c 16000026 295a022
  //   1680fff7 2002000a c 8fb00000 27bd0004 8fb30000 27bd0004 8fb40000 27bd0004 8fb50000 27bd0004 8fb60000
  //   27bd0004 8fa40000 27bd0004 8fa20000 27bd0004 42000018 201d07d0 27bdfffc afb00000 27bdfffc afb30000
  //   27bdfffc afb40000 27bdfffc afb50000 27bdfffc afb60000 27bdfffc afa40000 27bdfffc afa20000 20160002
  //   20140006 20150001 168020 108100 2149825 132020 20020022 c 16000026 295a022 1680fff7 2002000a c
  //   8fb00000 27bd0004 8fb30000 27bd0004 8fb40000 27bd0004 8fb50000 27bd0004 8fb60000 27bd0004 8fa40000
  //   27bd0004 8fa20000 27bd0004 42000018 201d07d0 27bdfffc afb00000 27bdfffc afb30000 27bdfffc afb40000
  //   27bdfffc afb50000 27bdfffc afb60000 27bdfffc afa40000 27bdfffc afa20000 20160003 20140006 20150001
  //   168020 108100 2149825 132020 20020022 c 1600ffa2 295a022 1680fff7 2002000a c 8fb00000 27bd0004
  //   8fb30000 27bd0004 8fb40000 27bd0004 8fb50000 27bd0004 8fb60000 27bd0004 8fa40000 27bd0004 8fa20000
  //   27bd0004 42000018
  //   中断信号采样参考电路
  //   中断信号采样参考电路
  //   Reset 
  //   Reset 
  //   Reset 
  //   中断信号源及指示电路规范（优先级3>2>1>CPU(0）)
endmodule

module Extcuit (
  input  [15:0] in_1,
  input  [5:0] in_2,
  input  [5:0] in_3,
  output [31:0] out_4
);

  wire comparator_1_eq, comparator_2_eq, comparator_3_eq, comparator_4_eq, comparator_5_eq, comparator_6_eq,
       comparator_7_eq, comparator_8_eq, comparator_9_eq, comparator_10_eq, comparator_11_eq,
       comparator_12_eq, comparator_13_eq, comparator_14_eq, or_2_out;
  wire [2:0] or_1_out;
  wire [31:0] bit_extender_1_out, bit_extender_2_out, multiplexer_1_out;

  Comparator #(.width(6)) comparator_1 (.a(6'b001000), .b(in_2), .eq(comparator_1_eq));  // open: gt, lt
  Comparator #(.width(6)) comparator_2 (.a(6'b001001), .b(in_2), .eq(comparator_2_eq));  // open: gt, lt
  Comparator #(.width(6)) comparator_3 (.a(6'b100011), .b(in_2), .eq(comparator_3_eq));  // open: gt, lt
  Comparator #(.width(6)) comparator_4 (.a(6'b101011), .b(in_2), .eq(comparator_4_eq));  // open: gt, lt
  Comparator #(.width(6)) comparator_5 (.a(6'b001010), .b(in_2), .eq(comparator_5_eq));  // open: gt, lt
  Comparator #(.width(6)) comparator_6 (.a(in_2), .b(6'b100100), .eq(comparator_6_eq));  // open: gt, lt
  Comparator #(.width(6)) comparator_7 (.a({6{1'b0}}), .b(in_3), .eq(comparator_7_eq));  // open: gt, lt
  Comparator #(.width(6)) comparator_8 (.a(6'b000010), .b(in_3), .eq(comparator_8_eq));  // open: gt, lt
  Comparator #(.width(6)) comparator_9 (.a(6'b000011), .b(in_3), .eq(comparator_9_eq));  // open: gt, lt
  Comparator #(.width(6)) comparator_10 (.a({6{1'b0}}), .b(in_2), .eq(comparator_10_eq));  // open: gt, lt
  Comparator #(.width(6)) comparator_11 (.a(6'b001100), .b(in_2), .eq(comparator_11_eq));  // open: gt, lt
  Comparator #(.width(6)) comparator_12 (.a(6'b001101), .b(in_2), .eq(comparator_12_eq));  // open: gt, lt
  Comparator #(.width(6)) comparator_13 (.a(6'b001110), .b(in_2), .eq(comparator_13_eq));  // open: gt, lt
  or or_1 (or_1_out[0], comparator_3_eq, comparator_1_eq, comparator_2_eq, comparator_4_eq, comparator_5_eq, comparator_6_eq);
  or or_2 (or_2_out, comparator_7_eq, comparator_8_eq, comparator_9_eq);
  or or_3 (or_1_out[1], comparator_11_eq, comparator_13_eq, comparator_12_eq);
  and and_1 (or_1_out[2], or_2_out, comparator_10_eq);
  assign bit_extender_1_out = {{16{in_1[15]}}, in_1};  // Bit_Extender bit_extender_1
  assign bit_extender_2_out = {{16{1'b0}}, in_1};  // Bit_Extender bit_extender_2
  Multiplexer #(.select(3), .width(32)) multiplexer_1 (
    .in1(bit_extender_1_out), .in2(bit_extender_2_out), .in4({{27{1'b0}}, in_1[10:6]}),
    .out(multiplexer_1_out), .sel(or_1_out));  // open: in0, in3, in5, in6, in7, en
  Comparator #(.width(6)) comparator_14 (.a(6'b000001), .b(in_2), .eq(comparator_14_eq));  // open: gt, lt
  Multiplexer #(.width(32)) multiplexer_2 (
    .in0(multiplexer_1_out), .in1({32{1'b0}}), .out(out_4), .sel(comparator_14_eq));  // open: en

  // Other names for the same wires on the sheet: data[15:0] = in_1; funct[5:0] = in_3; op[5:0] = in_2
endmodule

module AlusrcB (
  input  [5:0] op,
  input  [5:0] funct,
  output AlusrcB
);

  wire and_1_out, comparator_1_eq, comparator_2_eq, comparator_3_eq, comparator_4_eq, comparator_5_eq,
       comparator_6_eq, comparator_7_eq, comparator_8_eq, comparator_9_eq, comparator_10_eq,
       comparator_11_eq, comparator_12_eq, comparator_13_eq, comparator_14_eq, or_1_out, or_2_out;

  Comparator #(.width(6)) comparator_1 (.a(6'b001001), .b(op), .eq(comparator_1_eq));  // open: gt, lt
  Comparator #(.width(6)) comparator_2 (.a(6'b001000), .b(op), .eq(comparator_2_eq));  // open: gt, lt
  Comparator #(.width(6)) comparator_3 (.a(6'b001100), .b(op), .eq(comparator_3_eq));  // open: gt, lt
  Comparator #(.width(6)) comparator_4 (.a(6'b001101), .b(op), .eq(comparator_4_eq));  // open: gt, lt
  Comparator #(.width(6)) comparator_5 (.a(6'b100011), .b(op), .eq(comparator_5_eq));  // open: gt, lt
  Comparator #(.width(6)) comparator_6 (.a(6'b101011), .b(op), .eq(comparator_6_eq));  // open: gt, lt
  Comparator #(.width(6)) comparator_7 (.a(6'b001010), .b(op), .eq(comparator_7_eq));  // open: gt, lt
  Comparator #(.width(6)) comparator_8 (.a(op), .b(6'b001110), .eq(comparator_8_eq));  // open: gt, lt
  Comparator #(.width(6)) comparator_9 (.a(op), .b(6'b100100), .eq(comparator_9_eq));  // open: gt, lt
  or or_1 (or_1_out, comparator_1_eq, comparator_4_eq, comparator_2_eq, comparator_3_eq, comparator_9_eq, comparator_5_eq, comparator_6_eq, comparator_7_eq, comparator_8_eq);
  Comparator #(.width(6)) comparator_10 (.a(op), .b({6{1'b0}}), .eq(comparator_10_eq));  // open: gt, lt
  Comparator #(.width(6)) comparator_11 (.a({6{1'b0}}), .b(funct), .eq(comparator_11_eq));  // open: gt, lt
  Comparator #(.width(6)) comparator_12 (.a(6'b000011), .b(funct), .eq(comparator_12_eq));  // open: gt, lt
  Comparator #(.width(6)) comparator_13 (.a(6'b000010), .b(funct), .eq(comparator_13_eq));  // open: gt, lt
  Comparator #(.width(6)) comparator_14 (.a(funct), .b(6'b000110), .eq(comparator_14_eq));  // open: gt, lt
  Comparator #(.width(6)) comparator_15 ();  // open: a, b, gt, eq, lt
  Comparator #(.width(6)) comparator_16 ();  // open: a, b, gt, eq, lt
  or or_2 (or_2_out, comparator_11_eq, comparator_12_eq, comparator_13_eq);
  and and_1 (and_1_out, comparator_10_eq, or_2_out);
  or or_3 (AlusrcB, and_1_out, or_1_out);
endmodule

module Rfdin (
  input  [5:0] op,
  input  [5:0] funct,
  input  [31:0] dmout,
  input  [31:0] Aluout,
  input  [31:0] pc,
  output [31:0] out_6
);

  wire [2:0] comparator_1_eq;
  wire [31:0] adder_1_out, and_1_out;

  Adder #(.width(32)) adder_1 (.a(pc), .b(32'h4), .out(adder_1_out));  // open: cin, cout
  Comparator #(.width(6)) comparator_1 (.a(op), .b(6'b100100), .eq(comparator_1_eq[0]));  // open: gt, lt
  Comparator #(.width(6)) comparator_2 (.a(op), .b(6'b100011), .eq(comparator_1_eq[1]));  // open: gt, lt
  Comparator #(.width(6)) comparator_3 (.a(op), .b(6'b000011), .eq(comparator_1_eq[2]));  // open: gt, lt
  assign and_1_out = dmout & 32'hff;  // AND_Gate and_1, 32 bits wide
  Multiplexer #(.select(3), .width(32)) multiplexer_1 (
    .in0(Aluout), .in1(and_1_out), .in2(dmout), .in3(Aluout), .in4(adder_1_out), .in5(Aluout), .in6(Aluout),
    .in7(Aluout), .out(out_6), .sel(comparator_1_eq));  // open: en
endmodule

module Rfw (
  input  [5:0] op,
  input  [5:0] funct,
  output AlusrcB
);

  wire and_1_out, comparator_1_eq, comparator_2_eq, comparator_4_eq, comparator_5_eq, comparator_6_eq,
       comparator_8_eq, comparator_9_eq, comparator_10_eq, or_1_out, or_2_out, or_3_out;
  wire [5:0] undriven, undriven_2;

  Comparator #(.width(6)) comparator_1 (.a(6'b000001), .b(op), .eq(comparator_1_eq));  // open: gt, lt
  Comparator #(.width(6)) comparator_2 (.a(6'b000010), .b(op), .eq(comparator_2_eq));  // open: gt, lt
  Comparator #(.width(6)) comparator_3 (.b(op));  // open: a, gt, eq, lt
  Comparator #(.width(6)) comparator_4 (.a(6'b000100), .b(op), .eq(comparator_4_eq));  // open: gt, lt
  Comparator #(.width(6)) comparator_5 (.a(6'b000101), .b(op), .eq(comparator_5_eq));  // open: gt, lt
  Comparator #(.width(6)) comparator_6 (.a(6'b101011), .b(op), .eq(comparator_6_eq));  // open: gt, lt
  Comparator #(.width(6)) comparator_7 (.b(undriven));  // open: a, gt, eq, lt
  or or_1 (or_1_out, comparator_2_eq, comparator_1_eq, comparator_4_eq, comparator_5_eq, comparator_6_eq);
  Comparator #(.width(6)) comparator_8 (.a(op), .b({6{1'b0}}), .eq(comparator_8_eq));  // open: gt, lt
  Comparator #(.width(6)) comparator_9 (.a(6'b001000), .b(funct), .eq(comparator_9_eq));  // open: gt, lt
  Comparator #(.width(6)) comparator_10 (.a(6'b001100), .b(funct), .eq(comparator_10_eq));  // open: gt, lt
  Comparator #(.width(6)) comparator_11 (.a(undriven_2), .b(funct));  // open: gt, eq, lt
  Comparator #(.width(6)) comparator_12 ();  // open: a, b, gt, eq, lt
  Comparator #(.width(6)) comparator_13 ();  // open: a, b, gt, eq, lt
  Comparator #(.width(6)) comparator_14 ();  // open: a, b, gt, eq, lt
  or or_2 (or_2_out, comparator_9_eq, comparator_10_eq);
  and and_1 (and_1_out, comparator_8_eq, or_2_out);
  or or_3 (or_3_out, and_1_out, or_1_out);
  not not_1 (AlusrcB, or_3_out);
endmodule

module Dmsel (
  input  [5:0] op,
  output Dmsel
);

  wire comparator_1_eq, comparator_2_eq, comparator_3_eq;

  Comparator #(.width(6)) comparator_1 (.a(op), .b(6'b100011), .eq(comparator_1_eq));  // open: gt, lt
  Comparator #(.width(6)) comparator_2 (.a(op), .b(6'b100100), .eq(comparator_2_eq));  // open: gt, lt
  Comparator #(.width(6)) comparator_3 (.a(op), .b(6'b101011), .eq(comparator_3_eq));  // open: gt, lt
  or or_1 (Dmsel, comparator_1_eq, comparator_2_eq, comparator_3_eq);
endmodule

module pccuit (
  input  [5:0] op,
  input  [31:0] pc,
  input  [31:0] Aluout,
  input  [25:0] label,
  input  [31:0] rfd1,
  input  [5:0] funct,
  input  clk,
  input  pcen,
  output [31:0] newpc
);

  wire and_2_out, and_3_out, and_4_out, and_6_out, and_7_out, and_8_out, comparator_1_eq, comparator_2_eq,
       comparator_3_eq, comparator_4_eq, comparator_5_eq, comparator_6_eq, comparator_7_eq, comparator_8_eq,
       comparator_9_eq, comparator_10_eq, cond, not_1_out, or_4_out;
  wire [2:0] and_5_out;
  wire [15:0] \无条件总数_2_q , \无条件总数_3_q , \无条件总数_q ;
  wire [17:0] and_1_out, shifter_1_out;
  wire [25:0] shifter_2_out;
  wire [31:0] adder_1_out, adder_2_out, bit_extender_1_out, bit_extender_2_out, subtractor_1_out;

  assign and_1_out = label[17:0] & 18'hffff;  // AND_Gate and_1, 18 bits wide
  Adder #(.width(32)) adder_1 (.a(pc), .b(32'h4), .out(adder_1_out));  // open: cin, cout
  Comparator #(.width(6)) comparator_1 (.a(op), .b(6'b000010), .eq(comparator_1_eq));  // open: gt, lt
  Comparator #(.width(6)) comparator_2 (.a(op), .b(6'b000011), .eq(comparator_2_eq));  // open: gt, lt
  Shifter #(.width(18)) shifter_1 (.in(and_1_out), .\dist (5'b00010), .out(shifter_1_out));
  Shifter #(.width(26)) shifter_2 (.in(label), .\dist (5'b00010), .out(shifter_2_out));
  assign bit_extender_1_out = {{14{shifter_1_out[17]}}, shifter_1_out};  // Bit_Extender bit_extender_1
  or or_1 (and_5_out[1], comparator_1_eq, comparator_2_eq);
  assign bit_extender_2_out = {{6{shifter_2_out[25]}}, shifter_2_out};  // Bit_Extender bit_extender_2
  Comparator #(.width(32)) comparator_3 (.a(Aluout), .b({32{1'b0}}), .eq(comparator_3_eq));  // open: gt, lt
  Comparator #(.width(6)) comparator_4 (.a(op), .b(6'b000100), .eq(comparator_4_eq));  // open: gt, lt
  Comparator #(.width(6)) comparator_5 (.a(op), .b(6'b000101), .eq(comparator_5_eq));  // open: gt, lt
  Comparator #(.width(32)) comparator_6 (.a(Aluout), .b({32{1'b0}}), .eq(comparator_6_eq));  // open: gt, lt
  not not_1 (not_1_out, comparator_6_eq);
  Adder #(.width(32)) adder_2 (.a(bit_extender_1_out), .b(adder_1_out), .out(adder_2_out));  // open: cin, cout
  and and_2 (and_2_out, comparator_3_eq, comparator_4_eq);
  or or_2 (cond, comparator_4_eq, comparator_5_eq);
  and and_3 (and_3_out, comparator_5_eq, not_1_out);
  Comparator #(.width(32)) comparator_7 (.a(Aluout), .b(32'h1), .eq(comparator_7_eq));  // open: gt, lt
  Comparator #(.width(6)) comparator_8 (.a(op), .b(6'b000001), .eq(comparator_8_eq));  // open: gt, lt
  Subtractor #(.width(32)) subtractor_1 (
    .a({pc[31:28], label, 2'b00}), .b(32'h3000), .out(subtractor_1_out));  // open: bin, bout
  Comparator #(.width(6)) comparator_9 (.a(op), .b({6{1'b0}}), .eq(comparator_9_eq));  // open: gt, lt
  Comparator #(.width(6)) comparator_10 (.a(funct), .b(6'b001000), .eq(comparator_10_eq));  // open: gt, lt
  and and_4 (and_4_out, comparator_7_eq, comparator_8_eq);
  or or_3 (and_5_out[2], and_2_out, and_4_out, and_3_out);
  and and_5 (and_5_out[0], comparator_9_eq, comparator_10_eq);
  Multiplexer #(.select(3), .width(32)) multiplexer_1 (
    .in0(adder_1_out), .in1(rfd1), .in2(subtractor_1_out), .in3(adder_1_out), .in4(adder_2_out),
    .in5(adder_1_out), .in6(adder_1_out), .in7(adder_1_out), .out(newpc), .sel(and_5_out));  // open: en
  and and_6 (and_6_out, pcen, or_4_out);
  or or_4 (or_4_out, and_5_out[1], and_5_out[0]);
  and and_7 (and_7_out, pcen, and_5_out[2]);
  and and_8 (and_8_out, cond, pcen);
  Counter #(.width(16), .max('hffff)) \u_无条件总数  (
    .count(and_6_out), .Q(\无条件总数_q ), .clk(clk));  // open: load, D, carry, clr
  Counter #(.width(16), .max('hffff)) \u_无条件总数_2  (
    .count(and_7_out), .Q(\无条件总数_2_q ), .clk(clk));  // open: load, D, carry, clr
  Counter #(.width(16), .max('hffff)) \u_无条件总数_3  (
    .count(and_8_out), .Q(\无条件总数_3_q ), .clk(clk));  // open: load, D, carry, clr
  // Probe on \无条件总数_q 
  // Probe on \无条件总数_2_q 
  // Probe on \无条件总数_3_q 
endmodule

module test (
);

  wire [23:0] undriven;
  wire [31:0] rom_1_data;

  ROM #(.addrWidth(24), .dataWidth(32)) rom_1 (.addr(undriven), .data(rom_1_data));  // open: sel
endmodule

module Dmload (
  input  [5:0] op,
  output Dmload
);

  Comparator #(.width(6)) comparator_1 (.a(op), .b(6'b101011), .eq(Dmload));  // open: gt, lt
endmodule

module Dmstr (
  input  [5:0] op,
  output Dmsel
);

  wire comparator_1_eq, comparator_2_eq;

  Comparator #(.width(6)) comparator_1 (.a(op), .b(6'b100011), .eq(comparator_1_eq));  // open: gt, lt
  Comparator #(.width(6)) comparator_2 (.a(op), .b(6'b100100), .eq(comparator_2_eq));  // open: gt, lt
  or or_1 (Dmsel, comparator_1_eq, comparator_2_eq);
endmodule

module Aluop (
  input  [5:0] funct,
  input  [5:0] op,
  output [3:0] out_3
);

  wire comparator_1_eq;
  wire [3:0] rom_1_data, rom_2_data;

  Comparator #(.width(6)) comparator_1 (.a({6{1'b0}}), .b(op), .eq(comparator_1_eq));  // open: gt, lt
  ROM #(.addrWidth(6), .dataWidth(4)) rom_1 (.addr(funct), .data(rom_1_data));  // open: sel
  ROM #(.addrWidth(6), .dataWidth(4)) rom_2 (.addr(op), .data(rom_2_data));  // open: sel
  Multiplexer #(.width(4)) multiplexer_1 (
    .in0(rom_2_data), .in1(rom_1_data), .out(out_3), .sel(comparator_1_eq));  // open: en

  // Notes on the sheet:
  //   contents of rom_1 (hex, n*v repeats v):
  //   0 0 2 1 0 0 2 25*0 5 5 6 0 7 8 9 a 0 0 b c
  //   contents of rom_2 (hex, n*v repeats v):
  //   0 b 0 0 9 9 0 0 5 5 b 0 7 8 9
endmodule
