// Logisim project lab4.circ as structural Verilog: 11 circuits, main circuit main
module main (
  output out_1,
  output out_2,
  output out_3,
  output [15:0] out_4
);

  wire alu_1_p8, alusrcb_1_alusrcb, and_1_out, and_2_out, and_3_out, and_4_out, and_5_out, clock_1_out,
       comparator_1_eq, comparator_2_eq, comparator_3_eq, comparator_4_eq, comparator_5_eq, comparator_6_eq,
       comparator_7_eq, comparator_8_eq, comparator_9_eq, comparator_10_eq, comparator_11_eq,
       comparator_12_eq, comparator_13_eq, comparator_14_eq, comparator_15_eq, dmload_1_dmload,
       dmsel_1_dmsel, dmstr_1_dmsel, not_1_out, or_1_out, PCen, rfw_1_alusrcb, RST;
  wire [3:0] aluop_1_out_3, register_2_q;
  wire [4:0] multiplexer_1_out, multiplexer_3_out, registerfile_1_p6, registerfile_1_p7, rs, rt;
  wire [5:0] funct, OP;
  wire [15:6] imm;
  wire [31:0] alu_1_p2, Aluout, dmdout, extcuit_1_out_4, multiplexer_2_out, multiplexer_4_out,
       multiplexer_5_out, pc, pccuit_1_newpc, rfd1, rfd2, rfdin_1_out_6;
  wire [31:4] register_2_q_2;

  // Probe on OP
  Clock clock_1 (.out(clock_1_out));
  // Probe on rs
  // Probe on {imm, funct}
  Register #(.width(32)) register_1 (.D(pccuit_1_newpc), .en(PCen), .Q(pc), .clk(clock_1_out), .clr(RST));
  Comparator #(.width(6)) comparator_1 (.a(OP), .b(6'b000011), .eq(comparator_1_eq));  // open: gt, lt
  Button button_1 (.out(RST));
  Counter #(.width(16), .max('hffff)) counter_1 (
    .load(RST), .D({16{1'b0}}), .count(PCen), .Q(out_4), .clk(clock_1_out), .clr(RST));  // open: carry
  // Probe on rt
  // Probe on imm[15:11]
  pccuit pccuit_1 (
    .op(OP), .pc(pc), .Aluout(Aluout), .label({rs, rt, imm, funct}), .rfd1(rfd1), .funct(funct),
    .newpc(pccuit_1_newpc));
  Multiplexer #(.width(5)) multiplexer_1 (
    .in0(multiplexer_3_out), .in1({5{1'b1}}), .out(multiplexer_1_out), .sel(comparator_1_eq));  // open: en
  // Probe on out_4
  // Probe on imm[10:6]
  // Probe on funct
  ROM #(.addrWidth(24), .dataWidth(32)) rom_1 (.addr({2'b00, pc[23:2]}), .data({OP, rs, rt, imm, funct}));  // open: sel
  Comparator #(.width(6)) comparator_2 (.a(OP), .b(6'b001111), .eq(comparator_2_eq));  // open: gt, lt
  // Probe on {rs, rt, imm, funct}
  Multiplexer #(.width(32)) multiplexer_2 (
    .in0(rfdin_1_out_6), .in1({imm, funct, {16{1'b0}}}), .out(multiplexer_2_out), .sel(comparator_2_eq));  // open: en
  Multiplexer #(.width(5)) multiplexer_3 (
    .in0(rt), .in1(imm[15:11]), .out(multiplexer_3_out), .sel(comparator_3_eq));  // open: en
  Extcuit extcuit_1 (.in_1({imm, funct}), .in_2(OP), .in_3(funct), .out_4(extcuit_1_out_4));
  Comparator #(.width(6)) comparator_3 (.a({6{1'b0}}), .b(OP), .eq(comparator_3_eq));  // open: gt, lt
  Rfdin rfdin_1 (.op(OP), .funct(funct), .dmout(dmdout), .Aluout(Aluout), .pc(pc), .out_6(rfdin_1_out_6));
  Rfw rfw_1 (.op(OP), .funct(funct), .AlusrcB(rfw_1_alusrcb));
  Comparator #(.width(1)) comparator_4 (.a(and_3_out), .b(1'b1), .eq(comparator_4_eq));  // open: gt, lt
  Comparator #(.width(32)) comparator_5 (.a(rfd1), .b(32'ha), .eq(comparator_5_eq));  // open: gt, lt
  not not_1 (not_1_out, comparator_5_eq);
  // RegisterFile registerfile_1: pin names not known; wires that end beside it: {rs, rt, imm, funct}, multiplexer_2_out, clock_1_out, rfw_1_alusrcb, multiplexer_1_out, registerfile_1_p6, registerfile_1_p7, rfd1, rfd2, rfd1
  and and_1 (and_1_out, comparator_4_eq, not_1_out);
  Comparator #(.width(6)) comparator_6 (.a(funct), .b({6{1'b0}}), .eq(comparator_6_eq));  // open: gt, lt
  Comparator #(.width(6)) comparator_7 (.a(funct), .b(6'b000010), .eq(comparator_7_eq));  // open: gt, lt
  Comparator #(.width(6)) comparator_8 (.a(funct), .b(6'b000011), .eq(comparator_8_eq));  // open: gt, lt
  Comparator #(.width(6)) comparator_9 (.a(funct), .b(6'b000110), .eq(comparator_9_eq));  // open: gt, lt
  Comparator #(.width(6)) comparator_10 (.a(OP), .b({6{1'b0}}), .eq(comparator_10_eq));  // open: gt, lt
  Multiplexer #(.width(32)) multiplexer_4 (
    .in0(rfd1), .in1(rfd2), .out(multiplexer_4_out), .sel(and_4_out));  // open: en
  Aluop aluop_1 (.funct(funct), .op(OP), .out_3(aluop_1_out_3));
  Comparator #(.width(6)) comparator_11 (.a(funct), .b(6'b001100), .eq(comparator_11_eq));  // open: gt, lt
  Comparator #(.width(6)) comparator_12 (.a(OP), .b({6{1'b0}}), .eq(comparator_12_eq));  // open: gt, lt
  Register #(.width(32)) register_2 (
    .D(rfd2), .en(and_1_out), .Q({register_2_q_2, register_2_q}), .clk(clock_1_out), .clr(RST));
  Hex_Digit_Display hex_digit_display_1 (.value(register_2_q_2[31:28]));  // open: dp
  and and_2 (and_2_out, comparator_4_eq, comparator_5_eq);
  not not_2 (PCen, and_2_out);
  or or_1 (or_1_out, comparator_6_eq, comparator_7_eq, comparator_8_eq, comparator_9_eq);
  Multiplexer #(.width(32)) multiplexer_5 (
    .in0(rfd2), .in1(extcuit_1_out_4), .out(multiplexer_5_out), .sel(alusrcb_1_alusrcb));  // open: en
  AlusrcB alusrcb_1 (.op(OP), .funct(funct), .AlusrcB(alusrcb_1_alusrcb));
  and and_3 (and_3_out, comparator_11_eq, comparator_12_eq);
  Hex_Digit_Display hex_digit_display_2 (.value(register_2_q_2[27:24]));  // open: dp
  Hex_Digit_Display hex_digit_display_3 (.value(register_2_q_2[23:20]));  // open: dp
  // ALU alu_1: pin names not known; wires that end beside it: multiplexer_4_out, alu_1_p2, out_1, aluop_1_out_3, out_2, out_3, Aluout, alu_1_p8
  Multiplexer #(.width(5)) multiplexer_6 (
    .in0(rs), .in1(5'b00010), .out(registerfile_1_p6), .sel(and_3_out));  // open: en
  Multiplexer #(.width(5)) multiplexer_7 (
    .in0(rt), .in1(5'b00100), .out(registerfile_1_p7), .sel(and_3_out));  // open: en
  Hex_Digit_Display hex_digit_display_4 (.value(register_2_q_2[19:16]));  // open: dp
  Hex_Digit_Display hex_digit_display_5 (.value(register_2_q_2[15:12]));  // open: dp
  Comparator #(.width(6)) comparator_13 (.a(OP), .b({6{1'b0}}), .eq(comparator_13_eq));  // open: gt, lt
  Comparator #(.width(6)) comparator_14 (.a(funct), .b(6'b000110), .eq(comparator_14_eq));  // open: gt, lt
  and and_4 (and_4_out, or_1_out, comparator_10_eq);
  Dmload dmload_1 (.op(OP), .Dmload(dmload_1_dmload));
  Dmsel dmsel_1 (.op(OP), .Dmsel(dmsel_1_dmsel));
  Dmstr dmstr_1 (.op(OP), .Dmsel(dmstr_1_dmsel));
  Hex_Digit_Display hex_digit_display_6 (.value(register_2_q_2[11:8]));  // open: dp
  Hex_Digit_Display hex_digit_display_7 (.value(register_2_q_2[7:4]));  // open: dp
  // Probe on Aluout
  RAM #(.addrWidth(24), .dataWidth(32), .bus("separate")) ram_1 (
    .addr(Aluout[23:0]), .din(rfd2), .data(dmdout), .str(dmload_1_dmload), .sel(dmsel_1_dmsel),
    .clk(clock_1_out), .ld(dmstr_1_dmsel), .clr(RST));
  Comparator #(.width(6)) comparator_15 (.a(OP), .b(6'b101011), .eq(comparator_15_eq));  // open: gt, lt
  Hex_Digit_Display hex_digit_display_8 (.value(register_2_q));  // open: dp
  and and_5 (and_5_out, comparator_13_eq, comparator_14_eq);
  Multiplexer #(.width(32)) multiplexer_8 (
    .in0(multiplexer_5_out), .in1(rfd1), .out(alu_1_p2), .sel(and_5_out));  // open: en
  not not_3 (alu_1_p8, comparator_15_eq);

  // Other names for the same wires on the sheet: imm[5:0] = funct; shdmt[4:0] = imm[10:6]; rd[4:0] = imm[15:11]

  // Notes on the sheet:
  //         总复位
  //   contents of rom_1 (hex, n*v repeats v):
  //   20110001 8000c05 20110001 20120002 20130003 8000c09 20110001 20120002 20130003 8000c0d 20110001
  //   20120002 20130003 8000c11 20110001 20120002 20130003 c000cb8 20100001 20110001 118fc0 112020
  //   20020022 c 118882 12200001 8000c15 112020 20020022 c 20110001 118880 112020 20020022 c 12200001
  //   8000c1f 20110001 118fc0 112020 20020022 c 1188c3 112020 20020022 c 118903 112020 20020022 c 118903
  //   112020 20020022 c 118903 112020 20020022 c 118903 112020 20020022 c 118903 112020 20020022 c 118903
  //   112020 20020022 c 118903 112020 20020022 c 20100001 109fc0 139fc3 8021 2012000c 24160003 26100001
  //   3210000f 20080008 20090001 139900 2709825 132020 20020022 c 1094022 1500fff9 22100001 2018000f
  //   2188024 108700 20080008 20090001 139902 2709825 132021 20020022 c 1094022 1500fff9 108702 2c9b022
  //   12c00001 8000c50 4020 1084027 84400 3508ffff 82021 20020022 c 2010ffff 20110000 ae300000 22100001
  //   22310004 ae300000 22100001 22310004 ae300000 22100001 22310004 ae300000 22100001 22310004 ae300000
  //   22100001 22310004 ae300000 22100001 22310004 ae300000 22100001 22310004 ae300000 22100001 22310004
  //   ae300000 22100001 22310004 ae300000 22100001 22310004 ae300000 22100001 22310004 ae300000 22100001
  //   22310004 ae300000 22100001 22310004 ae300000 22100001 22310004 ae300000 22100001 22310004 ae300000
  //   22100001 22310004 22100001 8020 2011003c 8e130000 8e340000 274402a 11000002 ae330000 ae140000
  //   2231fffc 1611fff8 102020 20020022 c 22100004 2011003c 1611fff2 2002000a c 20100000 22100001 102020
  //   20020022 c 22100002 102020 20020022 c 22100003 102020 20020022 c 22100004 102020 20020022 c 22100005
  //   102020 20020022 c 22100006 102020 20020022 c 22100007 102020 20020022 c 22100008 102020 20020022
  //   20020022 c 3e00008
endmodule

module Extcuit (
  input  [15:0] in_1,
  input  [5:0] in_2,
  input  [5:0] in_3,
  output [31:0] out_4
);

  wire comparator_1_eq, comparator_2_eq, comparator_3_eq, comparator_4_eq, comparator_5_eq, comparator_6_eq,
       comparator_7_eq, comparator_8_eq, comparator_9_eq, comparator_10_eq, comparator_11_eq,
       comparator_12_eq, comparator_13_eq, or_2_out;
  wire [2:0] or_1_out;
  wire [31:0] bit_extender_1_out, bit_extender_2_out, multiplexer_1_out;

  Comparator #(.width(6)) comparator_1 (.a(6'b001000), .b(in_2), .eq(comparator_1_eq));  // open: gt, lt
  Comparator #(.width(6)) comparator_2 (.a(6'b001001), .b(in_2), .eq(comparator_2_eq));  // open: gt, lt
  Comparator #(.width(6)) comparator_3 (.a(6'b100011), .b(in_2), .eq(comparator_3_eq));  // open: gt, lt
  Comparator #(.width(6)) comparator_4 (.a(6'b101011), .b(in_2), .eq(comparator_4_eq));  // open: gt, lt
  Comparator #(.width(6)) comparator_5 (.a(6'b001010), .b(in_2), .eq(comparator_5_eq));  // open: gt, lt
  Comparator #(.width(6)) comparator_6 (.a(in_2), .b(6'b100100), .eq(comparator_6_eq));  // open: gt, lt
  Comparator #(.width(6)) comparator_7 (.a({6{1'b0}}), .b(in_3), .eq(comparator_7_eq));  // open: gt, lt
  Comparator #(.width(6)) comparator_8 (.a(6'b000010), .b(in_3), .eq(comparator_8_eq));  // open: gt, lt
  Comparator #(.width(6)) comparator_9 (.a(6'b000011), .b(in_3), .eq(comparator_9_eq));  // open: gt, lt
  Comparator #(.width(6)) comparator_10 (.a({6{1'b0}}), .b(in_2), .eq(comparator_10_eq));  // open: gt, lt
  Comparator #(.width(6)) comparator_11 (.a(6'b001100), .b(in_2), .eq(comparator_11_eq));  // open: gt, lt
  Comparator #(.width(6)) comparator_12 (.a(6'b001101), .b(in_2), .eq(comparator_12_eq));  // open: gt, lt
  or or_1 (or_1_out[0], comparator_3_eq, comparator_1_eq, comparator_2_eq, comparator_4_eq, comparator_5_eq, comparator_6_eq);
  or or_2 (or_2_out, comparator_7_eq, comparator_8_eq, comparator_9_eq);
  or or_3 (or_1_out[1], comparator_11_eq, comparator_12_eq);
  and and_1 (or_1_out[2], or_2_out, comparator_10_eq);
  assign bit_extender_1_out = {{16{in_1[15]}}, in_1};  // Bit_Extender bit_extender_1
  assign bit_extender_2_out = {{16{1'b0}}, in_1};  // Bit_Extender bit_extender_2
  Multiplexer #(.select(3), .width(32)) multiplexer_1 (
    .in1(bit_extender_1_out), .in2(bit_extender_2_out), .in4({{27{1'b0}}, in_1[10:6]}),
    .out(multiplexer_1_out), .sel(or_1_out));  // open: in0, in3, in5, in6, in7, en
  Comparator #(.width(6)) comparator_13 (.a(6'b000001), .b(in_2), .eq(comparator_13_eq));  // open: gt, lt
  Multiplexer #(.width(32)) multiplexer_2 (
    .in0(multiplexer_1_out), .in1({32{1'b0}}), .out(out_4), .sel(comparator_13_eq));  // open: en

  // Other names for the same wires on the sheet: data[15:0] = in_1; funct[5:0] = in_3; op[5:0] = in_2
endmodule

module AlusrcB (
  input  [5:0] op,
  input  [5:0] funct,
  output AlusrcB
);

  wire and_1_out, comparator_1_eq, comparator_2_eq, comparator_3_eq, comparator_4_eq, comparator_5_eq,
       comparator_6_eq, comparator_7_eq, comparator_8_eq, comparator_9_eq, comparator_10_eq,
       comparator_11_eq, comparator_12_eq, or_1_out, or_2_out;

  Comparator #(.width(6)) comparator_1 (.a(6'b001001), .b(op), .eq(comparator_1_eq));  // open: gt, lt
  Comparator #(.width(6)) comparator_2 (.a(6'b001000), .b(op), .eq(comparator_2_eq));  // open: gt, lt
  Comparator #(.width(6)) comparator_3 (.a(6'b001100), .b(op), .eq(comparator_3_eq));  // open: gt, lt
  Comparator #(.width(6)) comparator_4 (.a(6'b001101), .b(op), .eq(comparator_4_eq));  // open: gt, lt
  Comparator #(.width(6)) comparator_5 (.a(6'b100011), .b(op), .eq(comparator_5_eq));  // open: gt, lt
  Comparator #(.width(6)) comparator_6 (.a(6'b101011), .b(op), .eq(comparator_6_eq));  // open: gt, lt
  Comparator #(.width(6)) comparator_7 (.a(6'b001010), .b(op), .eq(comparator_7_eq));  // open: gt, lt
  or or_1 (or_1_out, comparator_1_eq, comparator_2_eq, comparator_3_eq, comparator_4_eq, comparator_5_eq, comparator_6_eq, comparator_7_eq);
  Comparator #(.width(6)) comparator_8 (.a(op), .b({6{1'b0}}), .eq(comparator_8_eq));  // open: gt, lt
  Comparator #(.width(6)) comparator_9 (.a({6{1'b0}}), .b(funct), .eq(comparator_9_eq));  // open: gt, lt
  Comparator #(.width(6)) comparator_10 (.a(6'b000011), .b(funct), .eq(comparator_10_eq));  // open: gt, lt
  Comparator #(.width(6)) comparator_11 (.a(6'b000010), .b(funct), .eq(comparator_11_eq));  // open: gt, lt
  Comparator #(.width(6)) comparator_12 (.a(funct), .b(6'b000110), .eq(comparator_12_eq));  // open: gt, lt
  Comparator #(.width(6)) comparator_13 ();  // open: a, b, gt, eq, lt
  Comparator #(.width(6)) comparator_14 ();  // open: a, b, gt, eq, lt
  or or_2 (or_2_out, comparator_9_eq, comparator_10_eq, comparator_11_eq);
  and and_1 (and_1_out, comparator_8_eq, or_2_out);
  or or_3 (AlusrcB, and_1_out, or_1_out);
endmodule

module Rfdin (
  input  [5:0] op,
  input  [5:0] funct,
  input  [31:0] dmout,
  input  [31:0] Aluout,
  input  [31:0] pc,
  output [31:0] out_6
);

  wire [2:0] comparator_1_eq;
  wire [31:0] adder_1_out, and_1_out;

  Adder #(.width(32)) adder_1 (.a(pc), .b(32'h4), .out(adder_1_out));  // open: cin, cout
  Comparator #(.width(6)) comparator_1 (.a(op), .b(6'b100100), .eq(comparator_1_eq[0]));  // open: gt, lt
  Comparator #(.width(6)) comparator_2 (.a(op), .b(6'b100011), .eq(comparator_1_eq[1]));  // open: gt, lt
  Comparator #(.width(6)) comparator_3 (.a(op), .b(6'b000011), .eq(comparator_1_eq[2]));  // open: gt, lt
  assign and_1_out = dmout & 32'hff;  // AND_Gate and_1, 32 bits wide
  Multiplexer #(.select(3), .width(32)) multiplexer_1 (
    .in0(Aluout), .in1(and_1_out), .in2(dmout), .in3(Aluout), .in4(adder_1_out), .in5(Aluout), .in6(Aluout),
    .in7(Aluout), .out(out_6), .sel(comparator_1_eq));  // open: en
endmodule

module Rfw (
  input  [5:0] op,
  input  [5:0] funct,
  output AlusrcB
);

  wire and_1_out, comparator_1_eq, comparator_2_eq, comparator_4_eq, comparator_5_eq, comparator_6_eq,
       comparator_8_eq, comparator_9_eq, comparator_10_eq, or_1_out, or_2_out, or_3_out;
  wire [5:0] undriven, undriven_2;

  Comparator #(.width(6)) comparator_1 (.a(6'b000001), .b(op), .eq(comparator_1_eq));  // open: gt, lt
  Comparator #(.width(6)) comparator_2 (.a(6'b000010), .b(op), .eq(comparator_2_eq));  // open: gt, lt
  Comparator #(.width(6)) comparator_3 (.b(op));  // open: a, gt, eq, lt
  Comparator #(.width(6)) comparator_4 (.a(6'b000100), .b(op), .eq(comparator_4_eq));  // open: gt, lt
  Comparator #(.width(6)) comparator_5 (.a(6'b000101), .b(op), .eq(comparator_5_eq));  // open: gt, lt
  Comparator #(.width(6)) comparator_6 (.a(6'b101011), .b(op), .eq(comparator_6_eq));  // open: gt, lt
  Comparator #(.width(6)) comparator_7 (.b(undriven));  // open: a, gt, eq, lt
  or or_1 (or_1_out, comparator_2_eq, comparator_1_eq, comparator_4_eq, comparator_5_eq, comparator_6_eq);
  Comparator #(.width(6)) comparator_8 (.a(op), .b({6{1'b0}}), .eq(comparator_8_eq));  // open: gt, lt
  Comparator #(.width(6)) comparator_9 (.a(6'b001000), .b(funct), .eq(comparator_9_eq));  // open: gt, lt
  Comparator #(.width(6)) comparator_10 (.a(6'b001100), .b(funct), .eq(comparator_10_eq));  // open: gt, lt
  Comparator #(.width(6)) comparator_11 (.a(undriven_2), .b(funct));  // open: gt, eq, lt
  Comparator #(.width(6)) comparator_12 ();  // open: a, b, gt, eq, lt
  Comparator #(.width(6)) comparator_13 ();  // open: a, b, gt, eq, lt
  Comparator #(.width(6)) comparator_14 ();  // open: a, b, gt, eq, lt
  or or_2 (or_2_out, comparator_9_eq, comparator_10_eq);
  and and_1 (and_1_out, comparator_8_eq, or_2_out);
  or or_3 (or_3_out, and_1_out, or_1_out);
  not not_1 (AlusrcB, or_3_out);
endmodule

module Dmsel (
  input  [5:0] op,
  output Dmsel
);

  wire comparator_1_eq, comparator_2_eq, comparator_3_eq;

  Comparator #(.width(6)) comparator_1 (.a(op), .b(6'b100011), .eq(comparator_1_eq));  // open: gt, lt
  Comparator #(.width(6)) comparator_2 (.a(op), .b(6'b100100), .eq(comparator_2_eq));  // open: gt, lt
  Comparator #(.width(6)) comparator_3 (.a(op), .b(6'b101011), .eq(comparator_3_eq));  // open: gt, lt
  or or_1 (Dmsel, comparator_1_eq, comparator_2_eq, comparator_3_eq);
endmodule

module pccuit (
  input  [5:0] op,
  input  [31:0] pc,
  input  [31:0] Aluout,
  input  [25:0] label,
  input  [31:0] rfd1,
  input  [5:0] funct,
  output [31:0] newpc
);

  wire and_2_out, and_3_out, and_4_out, comparator_1_eq, comparator_2_eq, comparator_3_eq, comparator_4_eq,
       comparator_5_eq, comparator_6_eq, comparator_7_eq, comparator_8_eq, comparator_9_eq, comparator_10_eq,
       not_1_out;
  wire [2:0] and_5_out;
  wire [17:0] and_1_out, shifter_1_out;
  wire [25:0] shifter_2_out;
  wire [31:0] adder_1_out, adder_2_out, bit_extender_1_out, bit_extender_2_out, subtractor_1_out;

  assign and_1_out = label[17:0] & 18'hffff;  // AND_Gate and_1, 18 bits wide
  Adder #(.width(32)) adder_1 (.a(pc), .b(32'h4), .out(adder_1_out));  // open: cin, cout
  Comparator #(.width(6)) comparator_1 (.a(op), .b(6'b000010), .eq(comparator_1_eq));  // open: gt, lt
  Comparator #(.width(6)) comparator_2 (.a(op), .b(6'b000011), .eq(comparator_2_eq));  // open: gt, lt
  Shifter #(.width(18)) shifter_1 (.in(and_1_out), .\dist (5'b00010), .out(shifter_1_out));
  Shifter #(.width(26)) shifter_2 (.in(label), .\dist (5'b00010), .out(shifter_2_out));
  assign bit_extender_1_out = {{14{shifter_1_out[17]}}, shifter_1_out};  // Bit_Extender bit_extender_1
  or or_1 (and_5_out[1], comparator_1_eq, comparator_2_eq);
  assign bit_extender_2_out = {{6{shifter_2_out[25]}}, shifter_2_out};  // Bit_Extender bit_extender_2
  Comparator #(.width(32)) comparator_3 (.a(Aluout), .b({32{1'b0}}), .eq(comparator_3_eq));  // open: gt, lt
  Comparator #(.width(6)) comparator_4 (.a(op), .b(6'b000100), .eq(comparator_4_eq));  // open: gt, lt
  Comparator #(.width(6)) comparator_5 (.a(op), .b(6'b000101), .eq(comparator_5_eq));  // open: gt, lt
  not not_1 (not_1_out, comparator_6_eq);
  Comparator #(.width(32)) comparator_6 (.a(Aluout), .b({32{1'b0}}), .eq(comparator_6_eq));  // open: gt, lt
  Adder #(.width(32)) adder_2 (.a(bit_extender_1_out), .b(adder_1_out), .out(adder_2_out));  // open: cin, cout
  and and_2 (and_2_out, comparator_3_eq, comparator_4_eq);
  and and_3 (and_3_out, comparator_5_eq, not_1_out);
  Comparator #(.width(32)) comparator_7 (.a(Aluout), .b(32'h1), .eq(comparator_7_eq));  // open: gt, lt
  Comparator #(.width(6)) comparator_8 (.a(op), .b(6'b000001), .eq(comparator_8_eq));  // open: gt, lt
  Subtractor #(.width(32)) subtractor_1 (
    .a({pc[31:28], label, 2'b00}), .b(32'h3000), .out(subtractor_1_out));  // open: bin, bout
  Comparator #(.width(6)) comparator_9 (.a(op), .b({6{1'b0}}), .eq(comparator_9_eq));  // open: gt, lt
  Comparator #(.width(6)) comparator_10 (.a(funct), .b(6'b001000), .eq(comparator_10_eq));  // open: gt, lt
  and and_4 (and_4_out, comparator_7_eq, comparator_8_eq);
  or or_2 (and_5_out[2], and_2_out, and_4_out, and_3_out);
  and and_5 (and_5_out[0], comparator_9_eq, comparator_10_eq);
  Multiplexer #(.select(3), .width(32)) multiplexer_1 (
    .in0(adder_1_out), .in1(rfd1), .in2(subtractor_1_out), .in3(adder_1_out), .in4(adder_2_out),
    .in5(adder_1_out), .in6(adder_1_out), .in7(adder_1_out), .out(newpc), .sel(and_5_out));  // open: en
endmodule

module test (
);

  wire [23:0] undriven;
  wire [31:0] rom_1_data;

  ROM #(.addrWidth(24), .dataWidth(32)) rom_1 (.addr(undriven), .data(rom_1_data));  // open: sel
endmodule

module Dmload (
  input  [5:0] op,
  output Dmload
);

  Comparator #(.width(6)) comparator_1 (.a(op), .b(6'b101011), .eq(Dmload));  // open: gt, lt
endmodule

module Dmstr (
  input  [5:0] op,
  output Dmsel
);

  wire comparator_1_eq, comparator_2_eq;

  Comparator #(.width(6)) comparator_1 (.a(op), .b(6'b100011), .eq(comparator_1_eq));  // open: gt, lt
  Comparator #(.width(6)) comparator_2 (.a(op), .b(6'b100100), .eq(comparator_2_eq));  // open: gt, lt
  or or_1 (Dmsel, comparator_1_eq, comparator_2_eq);
endmodule

module Aluop (
  input  [5:0] funct,
  input  [5:0] op,
  output [3:0] out_3
);

  wire comparator_1_eq;
  wire [3:0] rom_1_data, rom_2_data;

  Comparator #(.width(6)) comparator_1 (.a({6{1'b0}}), .b(op), .eq(comparator_1_eq));  // open: gt, lt
  ROM #(.addrWidth(6), .dataWidth(4)) rom_1 (.addr(funct), .data(rom_1_data));  // open: sel
  ROM #(.addrWidth(6), .dataWidth(4)) rom_2 (.addr(op), .data(rom_2_data));  // open: sel
  Multiplexer #(.width(4)) multiplexer_1 (
    .in0(rom_2_data), .in1(rom_1_data), .out(out_3), .sel(comparator_1_eq));  // open: en

  // Notes on the sheet:
  //   contents of rom_1 (hex, n*v repeats v):
  //   0 0 2 1 0 0 2 25*0 5 5 6 0 7 8 9 a 0 0 b c
  //   contents of rom_2 (hex, n*v repeats v):
  //   0 b 0 0 9 9 0 0 5 5 b 0 7 8
endmodule
